// Logisim project Bugputer.circ as structural Verilog: 10 circuits, main circuit main
module main (
  input  [7:0] in_1,
  input  in_2,
  input  [7:0] in_3,
  input  in_4,
  input  in_5,
  input  in_6,
  output [7:0] out_7
);

  Decoder decoder_1 (
    .in_1(in_1), .read(in_2));  // open: I0, I1, I2, I3, I4, I5, I6, I7, I8, I9, I10, I11, I12, I13, I14, I15
  Byte__15_Tick byte_15_tick_1 (.\input (in_3), .write(in_4), .reset(in_5), .read(in_6), .\output (out_7));
endmodule

module Switch__4_Tick (
  input  Input,
  input  Reset,
  output Output
);

  wire not_1_out, or_1_out, or_2_out, or_3_out, or_4_out;

  buf or_1 (or_1_out, Reset);  // OR_Gate
  buf or_2 (or_2_out, Input);  // OR_Gate
  or or_3 (or_3_out, or_1_out, Reset);
  not not_1 (not_1_out, or_3_out);
  or or_4 (or_4_out, Input, or_2_out, Output);
  and and_1 (Output, or_4_out, not_1_out);
endmodule

module Toggle__11_Tick (
  input  toggle,
  input  reset,
  output out_3
);

  wire and_1_out, and_2_out, and_3_out, not_1_out, not_2_out, or_1_out;

  not not_1 (not_1_out, toggle);
  not not_2 (not_2_out, toggle);
  Switch__4_Tick switch_4_tick_1 (.Input(and_1_out), .Reset(or_1_out), .Output(out_3));
  and and_1 (and_1_out, toggle, not_1_out);
  or or_1 (or_1_out, and_3_out, reset);
  and and_2 (and_2_out, not_2_out, out_3);
  and and_3 (and_3_out, and_2_out, toggle);
endmodule

module _8_bit_Counter__100_Tick (
  input  \input ,
  input  reset,
  output [7:0] count
);

  wire toggle_11_tick_1_out_3, toggle_11_tick_2_out_3, toggle_11_tick_3_out_3, toggle_11_tick_4_out_3,
       toggle_11_tick_5_out_3, toggle_11_tick_6_out_3, toggle_11_tick_7_out_3, toggle_11_tick_8_out_3;

  Toggle__11_Tick toggle_11_tick_1 (.toggle(\input ), .reset(reset), .out_3(toggle_11_tick_1_out_3));
  Toggle__11_Tick toggle_11_tick_2 (.toggle(toggle_11_tick_1_out_3), .reset(reset), .out_3(toggle_11_tick_2_out_3));
  Toggle__11_Tick toggle_11_tick_3 (.toggle(toggle_11_tick_2_out_3), .reset(reset), .out_3(toggle_11_tick_3_out_3));
  Toggle__11_Tick toggle_11_tick_4 (.toggle(toggle_11_tick_3_out_3), .reset(reset), .out_3(toggle_11_tick_4_out_3));
  Toggle__11_Tick toggle_11_tick_5 (.toggle(toggle_11_tick_4_out_3), .reset(reset), .out_3(toggle_11_tick_5_out_3));
  Toggle__11_Tick toggle_11_tick_6 (.toggle(toggle_11_tick_5_out_3), .reset(reset), .out_3(toggle_11_tick_6_out_3));
  Toggle__11_Tick toggle_11_tick_7 (.toggle(toggle_11_tick_8_out_3), .reset(reset), .out_3(toggle_11_tick_7_out_3));
  Toggle__11_Tick toggle_11_tick_8 (.toggle(toggle_11_tick_6_out_3), .reset(reset), .out_3(toggle_11_tick_8_out_3));
  not not_1 (count[0], toggle_11_tick_1_out_3);
  not not_2 (count[1], toggle_11_tick_2_out_3);
  not not_3 (count[2], toggle_11_tick_3_out_3);
  not not_4 (count[3], toggle_11_tick_4_out_3);
  not not_5 (count[4], toggle_11_tick_5_out_3);
  not not_6 (count[5], toggle_11_tick_6_out_3);
  not not_7 (count[6], toggle_11_tick_8_out_3);
  not not_8 (count[7], toggle_11_tick_7_out_3);
endmodule

module Byte__15_Tick (
  input  [7:0] \input ,
  input  write,
  input  reset,
  input  read,
  output [7:0] \output 
);

  wire and_1_out, and_2_out, and_3_out, and_4_out, and_5_out, and_6_out, and_7_out, and_8_out,
       switch_4_tick_1_output, switch_4_tick_2_output, switch_4_tick_3_output, switch_4_tick_4_output,
       switch_4_tick_5_output, switch_4_tick_6_output, switch_4_tick_7_output, switch_4_tick_8_output;

  and and_1 (and_1_out, \input [0], write);
  Switch__4_Tick switch_4_tick_1 (.Input(and_1_out), .Reset(reset), .Output(switch_4_tick_1_output));
  Switch__4_Tick switch_4_tick_2 (.Input(and_2_out), .Reset(reset), .Output(switch_4_tick_2_output));
  and and_2 (and_2_out, \input [1], write);
  and and_3 (and_3_out, \input [2], write);
  Switch__4_Tick switch_4_tick_3 (.Input(and_3_out), .Reset(reset), .Output(switch_4_tick_3_output));
  Switch__4_Tick switch_4_tick_4 (.Input(and_4_out), .Reset(reset), .Output(switch_4_tick_4_output));
  and and_4 (and_4_out, \input [3], write);
  and and_5 (and_5_out, \input [4], write);
  Switch__4_Tick switch_4_tick_5 (.Input(and_5_out), .Reset(reset), .Output(switch_4_tick_5_output));
  Switch__4_Tick switch_4_tick_6 (.Input(and_6_out), .Reset(reset), .Output(switch_4_tick_6_output));
  and and_6 (and_6_out, \input [5], write);
  Switch__4_Tick switch_4_tick_7 (.Input(and_7_out), .Reset(reset), .Output(switch_4_tick_7_output));
  and and_7 (and_7_out, \input [6], write);
  Switch__4_Tick switch_4_tick_8 (.Input(and_8_out), .Reset(reset), .Output(switch_4_tick_8_output));
  and and_8 (and_8_out, \input [7], write);
  and and_9 (\output [0], switch_4_tick_1_output, read);
  and and_10 (\output [1], switch_4_tick_2_output, read);
  and and_11 (\output [2], switch_4_tick_3_output, read);
  and and_12 (\output [3], switch_4_tick_4_output, read);
  and and_13 (\output [4], switch_4_tick_5_output, read);
  and and_14 (\output [5], switch_4_tick_6_output, read);
  and and_15 (\output [6], switch_4_tick_7_output, read);
  and and_16 (\output [7], switch_4_tick_8_output, read);
endmodule

module Decoder (
  input  [7:0] in_1,
  input  read,
  output I0,
  output I1,
  output I2,
  output I3,
  output I4,
  output I5,
  output I6,
  output I7,
  output I8,
  output I9,
  output I10,
  output I11,
  output I12,
  output I13,
  output I14,
  output I15
);

  wire and_1_out, and_3_out, and_5_out, and_6_out, and_9_out, and_10_out, and_13_out, and_14_out, and_17_out,
       and_19_out, and_21_out, and_23_out, and_25_out, and_27_out, and_29_out, and_31_out, not_1_out,
       not_2_out, not_3_out, not_4_out, not_5_out, not_6_out, not_7_out, not_8_out, not_9_out, not_10_out,
       not_11_out, not_12_out, not_13_out, not_14_out, not_15_out, not_16_out, not_17_out, not_18_out,
       not_19_out, not_20_out, not_21_out, not_22_out, not_23_out, not_24_out, not_25_out, not_26_out,
       not_27_out, not_28_out, not_29_out, not_30_out, not_31_out, not_32_out, not_33_out, not_34_out,
       not_35_out, not_36_out, not_37_out, not_38_out, not_39_out, not_40_out, not_41_out, not_42_out,
       not_43_out, not_44_out, not_45_out, not_46_out, not_47_out, not_48_out, not_49_out, not_50_out,
       not_51_out, not_52_out, not_53_out, not_54_out, not_55_out, not_56_out, not_57_out, not_58_out,
       not_59_out, not_60_out, not_61_out, not_62_out, not_63_out, not_64_out, not_65_out, not_66_out,
       not_67_out, not_68_out, not_69_out, not_70_out, not_71_out, not_72_out, not_73_out, not_74_out,
       not_75_out, not_76_out, not_77_out, not_78_out, not_79_out, not_80_out, not_81_out, not_82_out,
       not_83_out, not_84_out, not_85_out, not_86_out, not_87_out, not_88_out, not_89_out, not_90_out,
       not_91_out, not_92_out, not_93_out, not_94_out, not_95_out, not_96_out;

  not not_1 (not_1_out, in_1[0]);
  not not_2 (not_2_out, in_1[1]);
  not not_3 (not_3_out, in_1[2]);
  not not_4 (not_4_out, in_1[3]);
  not not_5 (not_5_out, in_1[4]);
  not not_6 (not_6_out, in_1[5]);
  not not_7 (not_7_out, in_1[6]);
  not not_8 (not_8_out, in_1[7]);
  not not_9 (not_9_out, in_1[0]);
  not not_10 (not_10_out, in_1[1]);
  not not_11 (not_11_out, in_1[2]);
  not not_12 (not_12_out, in_1[4]);
  not not_13 (not_13_out, in_1[5]);
  not not_14 (not_14_out, in_1[6]);
  not not_15 (not_15_out, in_1[7]);
  and and_1 (and_1_out, not_1_out, not_2_out, not_3_out, not_4_out, not_5_out, not_6_out, not_7_out, not_8_out);
  and and_2 (I0, and_1_out, read);
  and and_3 (and_3_out, not_9_out, not_10_out, not_11_out, in_1[3], not_12_out, not_13_out, not_14_out, not_15_out);
  and and_4 (I8, and_3_out, read);
  not not_16 (not_16_out, in_1[1]);
  not not_17 (not_17_out, in_1[2]);
  not not_18 (not_18_out, in_1[3]);
  and and_5 (and_5_out, in_1[0], not_16_out, not_17_out, not_18_out, not_19_out, not_20_out, not_21_out, not_22_out);
  not not_19 (not_19_out, in_1[4]);
  not not_20 (not_20_out, in_1[5]);
  not not_21 (not_21_out, in_1[6]);
  not not_22 (not_22_out, in_1[7]);
  not not_23 (not_23_out, in_1[1]);
  not not_24 (not_24_out, in_1[2]);
  and and_6 (and_6_out, in_1[0], not_23_out, not_24_out, in_1[3], not_25_out, not_26_out, not_27_out, not_28_out);
  not not_25 (not_25_out, in_1[4]);
  not not_26 (not_26_out, in_1[5]);
  not not_27 (not_27_out, in_1[6]);
  not not_28 (not_28_out, in_1[7]);
  and and_7 (I1, and_5_out, read);
  and and_8 (I9, and_6_out, read);
  not not_29 (not_29_out, in_1[0]);
  not not_30 (not_30_out, in_1[2]);
  not not_31 (not_31_out, in_1[3]);
  and and_9 (and_9_out, not_29_out, in_1[1], not_30_out, not_31_out, not_32_out, not_33_out, not_34_out, not_35_out);
  not not_32 (not_32_out, in_1[4]);
  not not_33 (not_33_out, in_1[5]);
  not not_34 (not_34_out, in_1[6]);
  not not_35 (not_35_out, in_1[7]);
  not not_36 (not_36_out, in_1[0]);
  not not_37 (not_37_out, in_1[2]);
  and and_10 (and_10_out, not_36_out, in_1[1], not_37_out, in_1[3], not_38_out, not_39_out, not_40_out, not_41_out);
  not not_38 (not_38_out, in_1[4]);
  not not_39 (not_39_out, in_1[5]);
  not not_40 (not_40_out, in_1[6]);
  not not_41 (not_41_out, in_1[7]);
  and and_11 (I2, and_9_out, read);
  and and_12 (I10, and_10_out, read);
  not not_42 (not_42_out, in_1[2]);
  not not_43 (not_43_out, in_1[3]);
  and and_13 (and_13_out, in_1[0], in_1[1], not_42_out, not_43_out, not_44_out, not_45_out, not_46_out, not_47_out);
  not not_44 (not_44_out, in_1[4]);
  not not_45 (not_45_out, in_1[5]);
  not not_46 (not_46_out, in_1[6]);
  not not_47 (not_47_out, in_1[7]);
  not not_48 (not_48_out, in_1[2]);
  and and_14 (and_14_out, in_1[0], in_1[1], not_48_out, in_1[3], not_49_out, not_50_out, not_51_out, not_52_out);
  not not_49 (not_49_out, in_1[4]);
  not not_50 (not_50_out, in_1[5]);
  not not_51 (not_51_out, in_1[6]);
  not not_52 (not_52_out, in_1[7]);
  and and_15 (I3, and_13_out, read);
  and and_16 (I11, and_14_out, read);
  not not_53 (not_53_out, in_1[0]);
  not not_54 (not_54_out, in_1[1]);
  not not_55 (not_55_out, in_1[3]);
  and and_17 (and_17_out, not_53_out, not_54_out, in_1[2], not_55_out, not_56_out, not_57_out, not_58_out, not_59_out);
  and and_18 (I4, and_17_out, read);
  not not_56 (not_56_out, in_1[4]);
  not not_57 (not_57_out, in_1[5]);
  not not_58 (not_58_out, in_1[6]);
  not not_59 (not_59_out, in_1[7]);
  not not_60 (not_60_out, in_1[0]);
  not not_61 (not_61_out, in_1[1]);
  and and_19 (and_19_out, not_60_out, not_61_out, in_1[2], in_1[3], not_62_out, not_63_out, not_64_out, not_65_out);
  and and_20 (I12, and_19_out, read);
  not not_62 (not_62_out, in_1[4]);
  not not_63 (not_63_out, in_1[5]);
  not not_64 (not_64_out, in_1[6]);
  not not_65 (not_65_out, in_1[7]);
  not not_66 (not_66_out, in_1[1]);
  not not_67 (not_67_out, in_1[3]);
  not not_68 (not_68_out, in_1[4]);
  not not_69 (not_69_out, in_1[5]);
  not not_70 (not_70_out, in_1[6]);
  not not_71 (not_71_out, in_1[7]);
  not not_72 (not_72_out, in_1[1]);
  not not_73 (not_73_out, in_1[4]);
  not not_74 (not_74_out, in_1[5]);
  not not_75 (not_75_out, in_1[6]);
  not not_76 (not_76_out, in_1[7]);
  and and_21 (and_21_out, in_1[0], not_66_out, in_1[2], not_67_out, not_68_out, not_69_out, not_70_out, not_71_out);
  and and_22 (I5, and_21_out, read);
  and and_23 (and_23_out, in_1[0], not_72_out, in_1[2], in_1[3], not_73_out, not_74_out, not_75_out, not_76_out);
  and and_24 (I13, and_23_out, read);
  not not_77 (not_77_out, in_1[0]);
  not not_78 (not_78_out, in_1[3]);
  not not_79 (not_79_out, in_1[4]);
  not not_80 (not_80_out, in_1[5]);
  not not_81 (not_81_out, in_1[6]);
  not not_82 (not_82_out, in_1[7]);
  not not_83 (not_83_out, in_1[0]);
  not not_84 (not_84_out, in_1[4]);
  not not_85 (not_85_out, in_1[5]);
  not not_86 (not_86_out, in_1[6]);
  not not_87 (not_87_out, in_1[7]);
  and and_25 (and_25_out, not_77_out, in_1[1], in_1[2], not_78_out, not_79_out, not_80_out, not_81_out, not_82_out);
  and and_26 (I6, and_25_out, read);
  and and_27 (and_27_out, not_83_out, in_1[1], in_1[2], in_1[3], not_84_out, not_85_out, not_86_out, not_87_out);
  and and_28 (I14, and_27_out, read);
  not not_88 (not_88_out, in_1[3]);
  not not_89 (not_89_out, in_1[4]);
  not not_90 (not_90_out, in_1[5]);
  not not_91 (not_91_out, in_1[6]);
  not not_92 (not_92_out, in_1[7]);
  not not_93 (not_93_out, in_1[4]);
  not not_94 (not_94_out, in_1[5]);
  not not_95 (not_95_out, in_1[6]);
  not not_96 (not_96_out, in_1[7]);
  and and_29 (and_29_out, in_1[0], in_1[1], in_1[2], not_88_out, not_89_out, not_90_out, not_91_out, not_92_out);
  and and_30 (I7, and_29_out, read);
  and and_31 (and_31_out, in_1[0], in_1[1], in_1[2], in_1[3], not_93_out, not_94_out, not_95_out, not_96_out);
  and and_32 (I15, and_31_out, read);

  // Other names for the same wires on the sheet: a[7:0] = in_1; r = read
endmodule

module Memory_Segment (
  input  [7:0] \input ,
  input  [7:0] read,
  output [7:0] \output 
);

  Byte__15_Tick byte_15_tick_1 ();  // open: input, write, reset, read, output
endmodule

module _8_byte_Memory (
  input  [7:0] \input ,
  input  write,
  input  [2:0] location,
  input  reset,
  input  read,
  output [7:0] \output 
);

  wire _0, _1, _2, _3, _4, _5, _6, _7, r0, r1, r2, r3, r4, r5, r6, r7, w0, w1, w2, w3, w4, w5, w6, w7;
  wire [7:0] byte_15_tick_1_output, byte_15_tick_2_output, byte_15_tick_3_output, byte_15_tick_4_output,
       byte_15_tick_5_output, byte_15_tick_6_output, byte_15_tick_7_output, byte_15_tick_8_output,
       byte_or_1_out_3, byte_or_2_out_3, byte_or_3_out_3, byte_or_4_out_3, byte_or_5_out_3, byte_or_7_out_3;

  Byte__15_Tick byte_15_tick_1 (.\input (\input ), .write(w0), .reset(r0), .read(_0), .\output (byte_15_tick_1_output));
  Byte__15_Tick byte_15_tick_2 (.\input (\input ), .write(w1), .reset(r1), .read(_1), .\output (byte_15_tick_2_output));
  Decoder_part #(.select(3)) decoder_1 (
    .out0(w0), .out1(w1), .out2(w2), .out3(w3), .out4(w4), .out5(w5), .out6(w6), .out7(w7), .sel(location),
    .en(write));
  Decoder_part #(.select(3)) decoder_2 (
    .out0(r0), .out1(r1), .out2(r2), .out3(r3), .out4(r4), .out5(r5), .out6(r6), .out7(r7), .sel(location),
    .en(reset));
  Byte__15_Tick byte_15_tick_3 (.\input (\input ), .write(w2), .reset(r2), .read(_2), .\output (byte_15_tick_3_output));
  Decoder_part #(.select(3)) decoder_3 (
    .out0(_0), .out1(_1), .out2(_2), .out3(_3), .out4(_4), .out5(_5), .out6(_6), .out7(_7), .sel(location),
    .en(read));
  Byte__15_Tick byte_15_tick_4 (.\input (\input ), .write(w3), .reset(r3), .read(_3), .\output (byte_15_tick_4_output));
  Byte__15_Tick byte_15_tick_5 (.\input (\input ), .write(w4), .reset(r4), .read(_4), .\output (byte_15_tick_5_output));
  Byte__15_Tick byte_15_tick_6 (.\input (\input ), .write(w6), .reset(r6), .read(_6), .\output (byte_15_tick_6_output));
  Byte__15_Tick byte_15_tick_7 (.\input (\input ), .write(w5), .reset(r5), .read(_5), .\output (byte_15_tick_7_output));
  Byte__15_Tick byte_15_tick_8 (.\input (\input ), .write(w7), .reset(r7), .read(_7), .\output (byte_15_tick_8_output));
  byte_OR byte_or_1 (.in_1(byte_15_tick_8_output), .in_2(byte_15_tick_6_output), .out_3(byte_or_1_out_3));
  byte_OR byte_or_2 (.in_1(byte_15_tick_7_output), .in_2(byte_15_tick_5_output), .out_3(byte_or_2_out_3));
  byte_OR byte_or_3 (.in_1(byte_15_tick_4_output), .in_2(byte_15_tick_3_output), .out_3(byte_or_3_out_3));
  byte_OR byte_or_4 (.in_1(byte_15_tick_2_output), .in_2(byte_15_tick_1_output), .out_3(byte_or_4_out_3));
  byte_OR byte_or_5 (.in_1(byte_or_1_out_3), .in_2(byte_or_2_out_3), .out_3(byte_or_5_out_3));
  byte_OR byte_or_6 (.in_1(byte_or_5_out_3), .in_2(byte_or_7_out_3), .out_3(\output ));
  byte_OR byte_or_7 (.in_1(byte_or_3_out_3), .in_2(byte_or_4_out_3), .out_3(byte_or_7_out_3));
endmodule

module byte_OR (
  input  [7:0] in_1,
  input  [7:0] in_2,
  output [7:0] out_3
);

  or or_1 (out_3[0], in_1[0], in_2[0]);
  or or_2 (out_3[1], in_1[1], in_2[1]);
  or or_3 (out_3[2], in_1[2], in_2[2]);
  or or_4 (out_3[3], in_1[3], in_2[3]);
  or or_5 (out_3[4], in_1[4], in_2[4]);
  or or_6 (out_3[5], in_1[5], in_2[5]);
  or or_7 (out_3[6], in_1[6], in_2[6]);
  or or_8 (out_3[7], in_1[7], in_2[7]);

  // Other names for the same wires on the sheet: a0 = in_1[0]; a1 = in_1[1]; a2 = in_1[2]; a3 = in_1[3]; a4 = in_1[4];
  //   a5 = in_1[5]; a6 = in_1[6]; a7 = in_1[7]; b0 = in_2[0]; b1 = in_2[1]; b2 = in_2[2]; b3 = in_2[3]; b4 = in_2[4];
  //   b5 = in_2[5]; b6 = in_2[6]; b7 = in_2[7]; _0 = out_3[0]; _1 = out_3[1]; _2 = out_3[2]; _3 = out_3[3];
  //   _4 = out_3[4]; _5 = out_3[5]; _6 = out_3[6]; _7 = out_3[7]
endmodule

module byte_AND (
  input  [7:0] \input ,
  input  pass,
  output [7:0] \output 
);

  and and_1 (\output [0], \input [0], pass);
  and and_2 (\output [1], \input [1], pass);
  and and_3 (\output [2], \input [2], pass);
  and and_4 (\output [3], \input [3], pass);
  and and_5 (\output [4], \input [4], pass);
  and and_6 (\output [5], \input [5], pass);
  and and_7 (\output [6], \input [6], pass);
  and and_8 (\output [7], \input [7], pass);
endmodule
