// Logisim project templeOS2.circ as structural Verilog: 20 circuits, main circuit main
module main (
  input  in_1,
  input  in_2,
  input  in_3,
  input  in_4,
  input  [7:0] in_5,
  input  [7:0] in_6,
  input  [7:0] in_7,
  input  in_8,
  input  in_9,
  input  in_10,
  input  [7:0] in_11,
  input  in_12,
  output [7:0] out_13,
  output [7:0] out_14,
  output [7:0] out_15,
  output [7:0] out_16
);

  wire and_1_out, byte_is_on_1_out_2, clock_1_out, clock_2_out, instruction_decoder_1_reset_byte,
       instruction_decoder_1_reset_byte__address, instruction_decoder_1_save_mem_byte__address,
       instruction_decoder_1_save_mem_byte__im1, instruction_decoder_1_save_mem_byte__im3,
       n4_bit_counter_1_out_3, n4_bit_counter_1_out_4, n4_bit_counter_1_out_5, n4_bit_counter_1_out_6,
       not_1_out, not_2_out, not_3_out, not_4_out, not_5_out, not_6_out, not_7_out, or_1_out, or_2_out,
       or_3_out, or_4_out, or_5_out;
  wire [7:0] byte_1_out, byte_path_1_out_3, byte_path_2_out_3, byte_path_3_out_3, byte_path_4_out_3,
       instruction_decoder_2_next_instruction__xxx, instruction_memory_1_out, instruction_memory_3_out,
       main_memory_byte_output, n2_byte_stream_converge_1_out_3, n2_byte_stream_converge_2_out_3,
       n2_byte_stream_converge_3_out_3, n2_byte_stream_converge_4_out_3, n8_byte_stream_converge_1_out_9,
       next_instruction_2_out, next_instruction_out, reset_byte_out_3;

  _4_bit_counter u_4_bit_counter_1 (
    .in_1(clock_1_out), .r(in_1), .out_3(n4_bit_counter_1_out_3), .out_4(n4_bit_counter_1_out_4),
    .out_5(n4_bit_counter_1_out_5), .out_6(n4_bit_counter_1_out_6));
  Clock clock_1 (.out(clock_1_out));
  or or_1 (or_1_out, in_8, n4_bit_counter_1_out_3);
  \byte  next_instruction (
    .in(byte_path_2_out_3), .store(n4_bit_counter_1_out_5), .out(next_instruction_out),
    .read(n4_bit_counter_1_out_3), .reset(n4_bit_counter_1_out_6));
  or or_2 (or_2_out, n4_bit_counter_1_out_4, in_4);
  _2_byte_stream_converge u_2_byte_stream_converge_1 (
    .in_1(next_instruction_out), .in_2(in_7), .out_3(n2_byte_stream_converge_1_out_3));
  instruction_decoder instruction_decoder_1 (
    .in_1(out_16), .next_instruction__xxx(out_13), .reset_byte(instruction_decoder_1_reset_byte),
    .reset_byte__Address(instruction_decoder_1_reset_byte__address),
    .save_mem_byte__Address(instruction_decoder_1_save_mem_byte__address),
    .save_mem_byte__IM1(instruction_decoder_1_save_mem_byte__im1),
    .save_mem_byte__IM3(instruction_decoder_1_save_mem_byte__im3));  // open: store_byte__Address, reset_byte__IM1, store_byte__IM1, IM1____IM2, add_IM1___IM2____IM3, sub_IM1___IM2____IM3, IM1___IM2____IM3, IM1___IM2____IM3_2, IM1___IM2____IM3_3, reset_IM3
  \byte  instruction (
    .in(n2_byte_stream_converge_1_out_3), .store(or_1_out), .out(out_16), .read(n4_bit_counter_1_out_5),
    .reset(or_2_out));
  \byte  memory_address (.in(in_11), .store(in_12), .out(out_14), .read(in_9), .reset(or_3_out));
  or or_3 (or_3_out, instruction_decoder_1_reset_byte__address, in_10);
  \byte  instruction_memory_1 (.out(instruction_memory_1_out));  // open: in, store, read, reset
  \byte  instruction_memory_2 ();  // open: in, store, out, read, reset
  \byte  instruction_memory_3 (.out(instruction_memory_3_out));  // open: in, store, read, reset
  or or_4 (or_4_out, instruction_decoder_1_save_mem_byte__im3, instruction_decoder_1_save_mem_byte__im1, instruction_decoder_1_save_mem_byte__address);
  _8_byte_stream_converge u_8_byte_stream_converge_1 (
    .in_1(out_14), .in_2({8{1'b0}}), .in_3({8{1'b0}}), .in_4({8{1'b0}}), .in_5({8{1'b0}}), .in_6({8{1'b0}}),
    .in_7({8{1'b0}}), .in_8({8{1'b0}}), .out_9(n8_byte_stream_converge_1_out_9));
  byte_path reset_byte (.location(out_14), .pass(instruction_decoder_1_reset_byte), .out_3(reset_byte_out_3));
  _2_byte_stream_converge u_2_byte_stream_converge_2 (
    .in_1(out_13), .in_2(in_5), .out_3(n2_byte_stream_converge_2_out_3));
  _8_byte_memory u_8_byte_memory_1 (
    .byte_input(n8_byte_stream_converge_1_out_9), .store(byte_path_1_out_3),
    .read(n2_byte_stream_converge_2_out_3), .reset(reset_byte_out_3), .byte_output(out_15));
  byte_path byte_path_1 (.location(out_14), .pass(or_4_out), .out_3(byte_path_1_out_3));
  byte_path byte_path_2 (.location(out_15), .out_3(byte_path_2_out_3));  // open: pass
  Clock clock_2 (.out(clock_2_out));
  or or_5 (or_5_out, in_2, clock_2_out);
  not not_1 (not_1_out, clock_2_out);
  not not_2 (not_2_out, not_3_out);
  not not_3 (not_3_out, not_4_out);
  not not_4 (not_4_out, not_5_out);
  not not_5 (not_5_out, or_5_out);
  \byte  next_instruction_2 (
    .in(n2_byte_stream_converge_3_out_3), .store(not_1_out), .out(next_instruction_2_out),
    .read(clock_2_out), .reset(not_2_out));
  _2_byte_stream_converge u_2_byte_stream_converge_3 (
    .in_1(byte_path_3_out_3), .in_2(byte_path_4_out_3), .out_3(n2_byte_stream_converge_3_out_3));
  byte_path byte_path_3 (.location(in_6), .pass(in_3), .out_3(byte_path_3_out_3));
  instruction_decoder instruction_decoder_2 (
    .in_1(next_instruction_2_out), .next_instruction__xxx(instruction_decoder_2_next_instruction__xxx));  // open: reset_byte, reset_byte__Address, store_byte__Address, save_mem_byte__Address, reset_byte__IM1, store_byte__IM1, save_mem_byte__IM1, IM1____IM2, save_mem_byte__IM3, add_IM1___IM2____IM3, sub_IM1___IM2____IM3, IM1___IM2____IM3, IM1___IM2____IM3_2, IM1___IM2____IM3_3, reset_IM3
  not not_6 (not_6_out, not_1_out);
  not not_7 (not_7_out, not_6_out);
  \byte  byte_1 (
    .in(instruction_decoder_2_next_instruction__xxx), .store(and_1_out), .out(byte_1_out), .read(not_1_out),
    .reset(not_7_out));
  and and_1 (and_1_out, or_5_out, byte_is_on_1_out_2);
  byte_path byte_path_4 (.location(main_memory_byte_output), .pass(not_1_out), .out_3(byte_path_4_out_3));
  byte_is_on byte_is_on_1 (.in_1(instruction_decoder_2_next_instruction__xxx), .out_2(byte_is_on_1_out_2));
  _2_byte_stream_converge u_2_byte_stream_converge_4 (
    .in_1(byte_1_out), .in_2({8{1'b0}}), .out_3(n2_byte_stream_converge_4_out_3));
  _8_byte_memory main_memory (
    .read(n2_byte_stream_converge_4_out_3), .byte_output(main_memory_byte_output));  // open: byte_input, store, reset
endmodule

module bit_memory (
  input  in_1,
  input  in_2,
  input  in_3,
  input  in_4,
  output out_5
);

  wire and_1_out, not_1_out, not_2_out, or_1_out, or_2_out;

  and and_1 (and_1_out, in_4, in_2);
  not not_1 (not_1_out, or_2_out);
  not not_2 (not_2_out, or_1_out);
  or or_1 (or_1_out, and_1_out, not_1_out);
  or or_2 (or_2_out, in_3, not_2_out);
  and and_2 (out_5, in_1, or_1_out);
endmodule

module \byte  (
  input  read,
  input  [7:0] in,
  input  store,
  input  reset,
  output [7:0] out
);

  bit_memory bit_memory_1 (.in_2(in[0]), .in_3(reset), .out_5(out[0]), .in_1(read), .in_4(store));
  bit_memory bit_memory_2 (.in_2(in[1]), .in_3(reset), .out_5(out[1]), .in_1(read), .in_4(store));
  bit_memory bit_memory_3 (.in_2(in[2]), .in_3(reset), .out_5(out[2]), .in_1(read), .in_4(store));
  bit_memory bit_memory_4 (.in_2(in[3]), .in_3(reset), .out_5(out[3]), .in_1(read), .in_4(store));
  bit_memory bit_memory_5 (.in_2(in[4]), .in_3(reset), .out_5(out[4]), .in_1(read), .in_4(store));
  bit_memory bit_memory_6 (.in_2(in[5]), .in_3(reset), .out_5(out[5]), .in_1(read), .in_4(store));
  bit_memory bit_memory_7 (.in_2(in[6]), .in_3(reset), .out_5(out[6]), .in_1(read), .in_4(store));
  bit_memory bit_memory_8 (.in_2(in[7]), .in_3(reset), .out_5(out[7]), .in_1(read), .in_4(store));
endmodule

module _8_byte_memory (
  input  [7:0] read,
  input  [7:0] byte_input,
  input  [7:0] store,
  input  [7:0] reset,
  output [7:0] byte_output
);

  wire [7:0] byte_1_out, byte_2_out, byte_3_out, byte_4_out, byte_5_out, byte_6_out, byte_7_out, byte_8_out;

  \byte  byte_1 (.in(byte_input), .store(store[0]), .out(byte_1_out), .read(read[0]), .reset(reset[0]));
  \byte  byte_2 (.in(byte_input), .store(store[1]), .out(byte_2_out), .read(read[1]), .reset(reset[1]));
  \byte  byte_3 (.in(byte_input), .store(store[2]), .out(byte_3_out), .read(read[2]), .reset(reset[2]));
  \byte  byte_4 (.in(byte_input), .store(store[3]), .out(byte_4_out), .read(read[3]), .reset(reset[3]));
  \byte  byte_5 (.in(byte_input), .store(store[4]), .out(byte_5_out), .read(read[4]), .reset(reset[4]));
  \byte  byte_6 (.in(byte_input), .store(store[5]), .out(byte_6_out), .read(read[5]), .reset(reset[5]));
  \byte  byte_7 (.in(byte_input), .store(store[7]), .out(byte_7_out), .read(read[7]), .reset(reset[7]));
  \byte  byte_8 (.in(byte_input), .store(store[6]), .out(byte_8_out), .read(read[6]), .reset(reset[6]));
  _8_byte_stream_converge u_8_byte_stream_converge_1 (
    .in_1(byte_7_out), .in_2(byte_8_out), .in_3(byte_6_out), .in_4(byte_5_out), .in_5(byte_4_out),
    .in_6(byte_3_out), .in_7(byte_2_out), .in_8(byte_1_out), .out_9(byte_output));
endmodule

module _8_byte_stream_converge (
  input  [7:0] in_1,
  input  [7:0] in_2,
  input  [7:0] in_3,
  input  [7:0] in_4,
  input  [7:0] in_5,
  input  [7:0] in_6,
  input  [7:0] in_7,
  input  [7:0] in_8,
  output [7:0] out_9
);

  wire [7:0] n2_byte_stream_converge_1_out_3, n2_byte_stream_converge_2_out_3,
       n2_byte_stream_converge_3_out_3, n2_byte_stream_converge_4_out_3, n2_byte_stream_converge_5_out_3,
       n2_byte_stream_converge_7_out_3;

  _2_byte_stream_converge u_2_byte_stream_converge_1 (
    .in_1(in_1), .in_2(in_2), .out_3(n2_byte_stream_converge_1_out_3));
  _2_byte_stream_converge u_2_byte_stream_converge_2 (
    .in_1(in_3), .in_2(in_4), .out_3(n2_byte_stream_converge_2_out_3));
  _2_byte_stream_converge u_2_byte_stream_converge_3 (
    .in_1(in_5), .in_2(in_6), .out_3(n2_byte_stream_converge_3_out_3));
  _2_byte_stream_converge u_2_byte_stream_converge_4 (
    .in_1(in_7), .in_2(in_8), .out_3(n2_byte_stream_converge_4_out_3));
  _2_byte_stream_converge u_2_byte_stream_converge_5 (
    .in_1(n2_byte_stream_converge_1_out_3), .in_2(n2_byte_stream_converge_2_out_3),
    .out_3(n2_byte_stream_converge_5_out_3));
  _2_byte_stream_converge u_2_byte_stream_converge_6 (
    .in_1(n2_byte_stream_converge_5_out_3), .in_2(n2_byte_stream_converge_7_out_3), .out_3(out_9));
  _2_byte_stream_converge u_2_byte_stream_converge_7 (
    .in_1(n2_byte_stream_converge_3_out_3), .in_2(n2_byte_stream_converge_4_out_3),
    .out_3(n2_byte_stream_converge_7_out_3));
endmodule

module _2_byte_stream_converge (
  input  [7:0] in_1,
  input  [7:0] in_2,
  output [7:0] out_3
);

  or or_1 (out_3[0], in_2[0], in_1[0]);
  or or_2 (out_3[1], in_2[1], in_1[1]);
  or or_3 (out_3[2], in_2[2], in_1[2]);
  or or_4 (out_3[3], in_2[3], in_1[3]);
  or or_5 (out_3[4], in_2[4], in_1[4]);
  or or_6 (out_3[5], in_2[5], in_1[5]);
  or or_7 (out_3[6], in_2[6], in_1[6]);
  or or_8 (out_3[7], in_2[7], in_1[7]);
endmodule

module byte_path (
  input  [7:0] location,
  input  pass,
  output [7:0] out_3
);

  and and_1 (out_3[0], location[0], pass);
  and and_2 (out_3[1], location[1], pass);
  and and_3 (out_3[2], location[2], pass);
  and and_4 (out_3[3], location[3], pass);
  and and_5 (out_3[4], location[4], pass);
  and and_6 (out_3[5], location[5], pass);
  and and_7 (out_3[6], location[6], pass);
  and and_8 (out_3[7], location[7], pass);
endmodule

module instruction_decoder (
  input  [7:0] in_1,
  output reset_byte,
  output reset_byte__Address,
  output store_byte__Address,
  output save_mem_byte__Address,
  output reset_byte__IM1,
  output [7:0] next_instruction__xxx,
  output store_byte__IM1,
  output save_mem_byte__IM1,
  output IM1____IM2,
  output save_mem_byte__IM3,
  output add_IM1___IM2____IM3,
  output sub_IM1___IM2____IM3,
  output IM1___IM2____IM3,
  output IM1___IM2____IM3_2,
  output IM1___IM2____IM3_3,
  output reset_IM3
);

  wire n1_tick_delay_1_out_2, n1_tick_delay_2_out_2, n1_tick_delay_3_out_2, n1_tick_delay_4_out_2,
       n1_tick_delay_5_out_2, n1_tick_delay_6_out_2, n1_tick_delay_7_out_2, n1_tick_delay_8_out_2,
       n1_tick_delay_9_out_2, n1_tick_delay_10_out_2, n1_tick_delay_11_out_2, n1_tick_delay_12_out_2,
       n1_tick_delay_13_out_2, n1_tick_delay_14_out_2, n1_tick_delay_15_out_2, n1_tick_delay_16_out_2,
       n1_tick_delay_17_out_2, n1_tick_delay_18_out_2, n1_tick_delay_19_out_2, n1_tick_delay_20_out_2,
       n1_tick_delay_21_out_2, n1_tick_delay_22_out_2, n1_tick_delay_23_out_2, n1_tick_delay_24_out_2,
       n1_tick_delay_25_out_2, n1_tick_delay_26_out_2, n1_tick_delay_27_out_2, n1_tick_delay_28_out_2,
       n1_tick_delay_29_out_2, n1_tick_delay_30_out_2, n1_tick_delay_31_out_2, n1_tick_delay_32_out_2,
       n2_tick_delay_1_out_2, n2_tick_delay_2_out_2, n2_tick_delay_3_out_2, n2_tick_delay_4_out_2,
       n2_tick_delay_5_out_2, n2_tick_delay_6_out_2, n2_tick_delay_7_out_2, n2_tick_delay_8_out_2,
       n2_tick_delay_9_out_2, n2_tick_delay_10_out_2, n2_tick_delay_11_out_2, n2_tick_delay_12_out_2,
       n2_tick_delay_13_out_2, n2_tick_delay_14_out_2, n2_tick_delay_15_out_2, n2_tick_delay_16_out_2,
       n2_tick_delay_17_out_2, n2_tick_delay_18_out_2, n2_tick_delay_19_out_2, n2_tick_delay_20_out_2,
       n2_tick_delay_21_out_2, n2_tick_delay_22_out_2, n2_tick_delay_23_out_2, n2_tick_delay_24_out_2,
       n2_tick_delay_25_out_2, n2_tick_delay_26_out_2, n2_tick_delay_27_out_2, n2_tick_delay_28_out_2,
       not_1_out, not_2_out, not_3_out, not_4_out, not_5_out, not_6_out, not_7_out, not_8_out, not_9_out,
       not_10_out, not_11_out, not_12_out, not_13_out, not_14_out, not_15_out, not_16_out, not_17_out,
       not_18_out, not_19_out, not_20_out, not_21_out, not_22_out, not_23_out, not_24_out, not_25_out,
       not_26_out, not_27_out, not_28_out;
  wire [7:0] n4_bit_decoder_1_out_2;

  _4_bit_decoder u_4_bit_decoder_1 (.in_1(in_1[7:4]), .out_2({next_instruction__xxx, n4_bit_decoder_1_out_2}));
  _1_tick_delay u_1_tick_delay_1 (.in_1(in_1[0]), .out_2(n1_tick_delay_1_out_2));
  _1_tick_delay u_1_tick_delay_2 (.in_1(in_1[1]), .out_2(n1_tick_delay_2_out_2));
  _1_tick_delay u_1_tick_delay_3 (.in_1(in_1[0]), .out_2(n1_tick_delay_3_out_2));
  _1_tick_delay u_1_tick_delay_4 (.in_1(in_1[1]), .out_2(n1_tick_delay_4_out_2));
  _1_tick_delay u_1_tick_delay_5 (.in_1(in_1[2]), .out_2(n1_tick_delay_5_out_2));
  _1_tick_delay u_1_tick_delay_6 (.in_1(in_1[0]), .out_2(n1_tick_delay_6_out_2));
  _1_tick_delay u_1_tick_delay_7 (.in_1(in_1[2]), .out_2(n1_tick_delay_7_out_2));
  _1_tick_delay u_1_tick_delay_8 (.in_1(in_1[1]), .out_2(n1_tick_delay_8_out_2));
  _1_tick_delay u_1_tick_delay_9 (.in_1(in_1[2]), .out_2(n1_tick_delay_9_out_2));
  _1_tick_delay u_1_tick_delay_10 (.in_1(in_1[0]), .out_2(n1_tick_delay_10_out_2));
  _1_tick_delay u_1_tick_delay_11 (.in_1(in_1[1]), .out_2(n1_tick_delay_11_out_2));
  _1_tick_delay u_1_tick_delay_12 (.in_1(in_1[2]), .out_2(n1_tick_delay_12_out_2));
  _1_tick_delay u_1_tick_delay_13 (.in_1(in_1[3]), .out_2(n1_tick_delay_13_out_2));
  _1_tick_delay u_1_tick_delay_14 (.in_1(in_1[0]), .out_2(n1_tick_delay_14_out_2));
  _1_tick_delay u_1_tick_delay_15 (.in_1(in_1[3]), .out_2(n1_tick_delay_15_out_2));
  _1_tick_delay u_1_tick_delay_16 (.in_1(in_1[1]), .out_2(n1_tick_delay_16_out_2));
  _1_tick_delay u_1_tick_delay_17 (.in_1(in_1[3]), .out_2(n1_tick_delay_17_out_2));
  _1_tick_delay u_1_tick_delay_18 (.in_1(in_1[0]), .out_2(n1_tick_delay_18_out_2));
  _1_tick_delay u_1_tick_delay_19 (.in_1(in_1[1]), .out_2(n1_tick_delay_19_out_2));
  _1_tick_delay u_1_tick_delay_20 (.in_1(in_1[3]), .out_2(n1_tick_delay_20_out_2));
  _1_tick_delay u_1_tick_delay_21 (.in_1(in_1[2]), .out_2(n1_tick_delay_21_out_2));
  _1_tick_delay u_1_tick_delay_22 (.in_1(in_1[3]), .out_2(n1_tick_delay_22_out_2));
  _1_tick_delay u_1_tick_delay_23 (.in_1(in_1[0]), .out_2(n1_tick_delay_23_out_2));
  _1_tick_delay u_1_tick_delay_24 (.in_1(in_1[2]), .out_2(n1_tick_delay_24_out_2));
  _1_tick_delay u_1_tick_delay_25 (.in_1(in_1[3]), .out_2(n1_tick_delay_25_out_2));
  _1_tick_delay u_1_tick_delay_26 (.in_1(in_1[1]), .out_2(n1_tick_delay_26_out_2));
  _1_tick_delay u_1_tick_delay_27 (.in_1(in_1[2]), .out_2(n1_tick_delay_27_out_2));
  _1_tick_delay u_1_tick_delay_28 (.in_1(in_1[3]), .out_2(n1_tick_delay_28_out_2));
  _1_tick_delay u_1_tick_delay_29 (.in_1(in_1[0]), .out_2(n1_tick_delay_29_out_2));
  _1_tick_delay u_1_tick_delay_30 (.in_1(in_1[1]), .out_2(n1_tick_delay_30_out_2));
  _1_tick_delay u_1_tick_delay_31 (.in_1(in_1[2]), .out_2(n1_tick_delay_31_out_2));
  _1_tick_delay u_1_tick_delay_32 (.in_1(in_1[3]), .out_2(n1_tick_delay_32_out_2));
  not not_1 (not_1_out, in_1[1]);
  _2_tick_delay u_2_tick_delay_1 (.in_1(not_1_out), .out_2(n2_tick_delay_1_out_2));
  and and_1 (reset_byte, n1_tick_delay_1_out_2, n2_tick_delay_1_out_2, n2_tick_delay_2_out_2, n2_tick_delay_3_out_2);
  not not_2 (not_2_out, in_1[2]);
  _2_tick_delay u_2_tick_delay_2 (.in_1(not_2_out), .out_2(n2_tick_delay_2_out_2));
  not not_3 (not_3_out, in_1[3]);
  _2_tick_delay u_2_tick_delay_3 (.in_1(not_3_out), .out_2(n2_tick_delay_3_out_2));
  not not_4 (not_4_out, in_1[0]);
  _2_tick_delay u_2_tick_delay_4 (.in_1(not_4_out), .out_2(n2_tick_delay_4_out_2));
  and and_2 (reset_byte__Address, n2_tick_delay_4_out_2, n1_tick_delay_2_out_2, n2_tick_delay_5_out_2, n2_tick_delay_6_out_2);
  not not_5 (not_5_out, in_1[2]);
  _2_tick_delay u_2_tick_delay_5 (.in_1(not_5_out), .out_2(n2_tick_delay_5_out_2));
  not not_6 (not_6_out, in_1[3]);
  _2_tick_delay u_2_tick_delay_6 (.in_1(not_6_out), .out_2(n2_tick_delay_6_out_2));
  and and_3 (store_byte__Address, n1_tick_delay_3_out_2, n1_tick_delay_4_out_2, n2_tick_delay_7_out_2, n2_tick_delay_8_out_2);
  not not_7 (not_7_out, in_1[2]);
  _2_tick_delay u_2_tick_delay_7 (.in_1(not_7_out), .out_2(n2_tick_delay_7_out_2));
  _2_tick_delay u_2_tick_delay_8 (.in_1(not_8_out), .out_2(n2_tick_delay_8_out_2));
  not not_8 (not_8_out, in_1[3]);
  _2_tick_delay u_2_tick_delay_9 (.in_1(not_9_out), .out_2(n2_tick_delay_9_out_2));
  not not_9 (not_9_out, in_1[0]);
  _2_tick_delay u_2_tick_delay_10 (.in_1(not_10_out), .out_2(n2_tick_delay_10_out_2));
  not not_10 (not_10_out, in_1[1]);
  and and_4 (save_mem_byte__Address, n2_tick_delay_9_out_2, n2_tick_delay_10_out_2, n1_tick_delay_5_out_2, n2_tick_delay_11_out_2);
  not not_11 (not_11_out, in_1[3]);
  _2_tick_delay u_2_tick_delay_11 (.in_1(not_11_out), .out_2(n2_tick_delay_11_out_2));
  not not_12 (not_12_out, in_1[1]);
  _2_tick_delay u_2_tick_delay_12 (.in_1(not_12_out), .out_2(n2_tick_delay_12_out_2));
  and and_5 (reset_byte__IM1, n1_tick_delay_6_out_2, n2_tick_delay_12_out_2, n1_tick_delay_7_out_2, n2_tick_delay_13_out_2);
  _2_tick_delay u_2_tick_delay_13 (.in_1(not_13_out), .out_2(n2_tick_delay_13_out_2));
  not not_13 (not_13_out, in_1[3]);
  _2_tick_delay u_2_tick_delay_14 (.in_1(not_14_out), .out_2(n2_tick_delay_14_out_2));
  not not_14 (not_14_out, in_1[0]);
  and and_6 (store_byte__IM1, n2_tick_delay_14_out_2, n1_tick_delay_8_out_2, n1_tick_delay_9_out_2, n2_tick_delay_15_out_2);
  _2_tick_delay u_2_tick_delay_15 (.in_1(not_15_out), .out_2(n2_tick_delay_15_out_2));
  not not_15 (not_15_out, in_1[3]);
  and and_7 (save_mem_byte__IM1, n1_tick_delay_10_out_2, n1_tick_delay_11_out_2, n1_tick_delay_12_out_2, n2_tick_delay_16_out_2);
  _2_tick_delay u_2_tick_delay_16 (.in_1(not_16_out), .out_2(n2_tick_delay_16_out_2));
  not not_16 (not_16_out, in_1[3]);
  not not_17 (not_17_out, in_1[0]);
  _2_tick_delay u_2_tick_delay_17 (.in_1(not_17_out), .out_2(n2_tick_delay_17_out_2));
  not not_18 (not_18_out, in_1[1]);
  _2_tick_delay u_2_tick_delay_18 (.in_1(not_18_out), .out_2(n2_tick_delay_18_out_2));
  and and_8 (IM1____IM2, n2_tick_delay_17_out_2, n2_tick_delay_18_out_2, n2_tick_delay_19_out_2, n1_tick_delay_13_out_2);
  not not_19 (not_19_out, in_1[2]);
  _2_tick_delay u_2_tick_delay_19 (.in_1(not_19_out), .out_2(n2_tick_delay_19_out_2));
  not not_20 (not_20_out, in_1[1]);
  _2_tick_delay u_2_tick_delay_20 (.in_1(not_20_out), .out_2(n2_tick_delay_20_out_2));
  and and_9 (save_mem_byte__IM3, n1_tick_delay_14_out_2, n2_tick_delay_20_out_2, n2_tick_delay_21_out_2, n1_tick_delay_15_out_2);
  not not_21 (not_21_out, in_1[2]);
  _2_tick_delay u_2_tick_delay_21 (.in_1(not_21_out), .out_2(n2_tick_delay_21_out_2));
  not not_22 (not_22_out, in_1[0]);
  _2_tick_delay u_2_tick_delay_22 (.in_1(not_22_out), .out_2(n2_tick_delay_22_out_2));
  and and_10 (add_IM1___IM2____IM3, n2_tick_delay_22_out_2, n1_tick_delay_16_out_2, n2_tick_delay_23_out_2, n1_tick_delay_17_out_2);
  _2_tick_delay u_2_tick_delay_23 (.in_1(not_23_out), .out_2(n2_tick_delay_23_out_2));
  not not_23 (not_23_out, in_1[2]);
  and and_11 (sub_IM1___IM2____IM3, n1_tick_delay_18_out_2, n1_tick_delay_19_out_2, n2_tick_delay_24_out_2, n1_tick_delay_20_out_2);
  not not_24 (not_24_out, in_1[2]);
  _2_tick_delay u_2_tick_delay_24 (.in_1(not_24_out), .out_2(n2_tick_delay_24_out_2));
  not not_25 (not_25_out, in_1[0]);
  _2_tick_delay u_2_tick_delay_25 (.in_1(not_25_out), .out_2(n2_tick_delay_25_out_2));
  _2_tick_delay u_2_tick_delay_26 (.in_1(not_26_out), .out_2(n2_tick_delay_26_out_2));
  not not_26 (not_26_out, in_1[1]);
  and and_12 (IM1___IM2____IM3, n2_tick_delay_25_out_2, n2_tick_delay_26_out_2, n1_tick_delay_21_out_2, n1_tick_delay_22_out_2);
  _2_tick_delay u_2_tick_delay_27 (.in_1(not_27_out), .out_2(n2_tick_delay_27_out_2));
  not not_27 (not_27_out, in_1[1]);
  and and_13 (IM1___IM2____IM3_2, n1_tick_delay_23_out_2, n2_tick_delay_27_out_2, n1_tick_delay_24_out_2, n1_tick_delay_25_out_2);
  not not_28 (not_28_out, in_1[0]);
  _2_tick_delay u_2_tick_delay_28 (.in_1(not_28_out), .out_2(n2_tick_delay_28_out_2));
  and and_14 (IM1___IM2____IM3_3, n2_tick_delay_28_out_2, n1_tick_delay_26_out_2, n1_tick_delay_27_out_2, n1_tick_delay_28_out_2);
  and and_15 (reset_IM3, n1_tick_delay_29_out_2, n1_tick_delay_30_out_2, n1_tick_delay_31_out_2, n1_tick_delay_32_out_2);
endmodule

module _4_bit_decoder (
  input  [3:0] in_1,
  output [15:0] out_2
);

  wire not_1_out, not_2_out, not_3_out, not_4_out, not_5_out, not_6_out, not_7_out, not_8_out, not_9_out,
       not_10_out, not_11_out, not_12_out, not_13_out, not_14_out, not_15_out, not_16_out, not_17_out,
       not_18_out, not_19_out, not_20_out, not_21_out, not_22_out, not_23_out, not_24_out, not_25_out,
       not_26_out, not_27_out, not_28_out, not_29_out, not_30_out, not_31_out, not_32_out;

  not not_1 (not_1_out, in_1[0]);
  not not_2 (not_2_out, in_1[1]);
  and and_1 (out_2[0], not_1_out, not_2_out, not_3_out, not_4_out);
  not not_3 (not_3_out, in_1[2]);
  not not_4 (not_4_out, in_1[3]);
  not not_5 (not_5_out, in_1[1]);
  and and_2 (out_2[1], in_1[0], not_5_out, not_6_out, not_7_out);
  not not_6 (not_6_out, in_1[2]);
  not not_7 (not_7_out, in_1[3]);
  not not_8 (not_8_out, in_1[0]);
  and and_3 (out_2[2], not_8_out, in_1[1], not_9_out, not_10_out);
  not not_9 (not_9_out, in_1[2]);
  not not_10 (not_10_out, in_1[3]);
  and and_4 (out_2[3], in_1[0], in_1[1], not_11_out, not_12_out);
  not not_11 (not_11_out, in_1[2]);
  not not_12 (not_12_out, in_1[3]);
  not not_13 (not_13_out, in_1[0]);
  not not_14 (not_14_out, in_1[1]);
  and and_5 (out_2[4], not_13_out, not_14_out, in_1[2], not_15_out);
  not not_15 (not_15_out, in_1[3]);
  not not_16 (not_16_out, in_1[1]);
  and and_6 (out_2[5], in_1[0], not_16_out, in_1[2], not_17_out);
  not not_17 (not_17_out, in_1[3]);
  not not_18 (not_18_out, in_1[0]);
  and and_7 (out_2[6], not_18_out, in_1[1], in_1[2], not_19_out);
  not not_19 (not_19_out, in_1[3]);
  and and_8 (out_2[7], in_1[0], in_1[1], in_1[2], not_20_out);
  not not_20 (not_20_out, in_1[3]);
  not not_21 (not_21_out, in_1[0]);
  not not_22 (not_22_out, in_1[1]);
  and and_9 (out_2[8], not_21_out, not_22_out, not_23_out, in_1[3]);
  not not_23 (not_23_out, in_1[2]);
  not not_24 (not_24_out, in_1[1]);
  and and_10 (out_2[9], in_1[0], not_24_out, not_25_out, in_1[3]);
  not not_25 (not_25_out, in_1[2]);
  not not_26 (not_26_out, in_1[0]);
  and and_11 (out_2[10], not_26_out, in_1[1], not_27_out, in_1[3]);
  not not_27 (not_27_out, in_1[2]);
  and and_12 (out_2[11], in_1[0], in_1[1], not_28_out, in_1[3]);
  not not_28 (not_28_out, in_1[2]);
  not not_29 (not_29_out, in_1[0]);
  not not_30 (not_30_out, in_1[1]);
  and and_13 (out_2[12], not_29_out, not_30_out, in_1[2], in_1[3]);
  not not_31 (not_31_out, in_1[1]);
  and and_14 (out_2[13], in_1[0], not_31_out, in_1[2], in_1[3]);
  not not_32 (not_32_out, in_1[0]);
  and and_15 (out_2[14], not_32_out, in_1[1], in_1[2], in_1[3]);
  and and_16 (out_2[15], in_1[0], in_1[1], in_1[2], in_1[3]);
endmodule

module byte_is_on (
  input  [7:0] in_1,
  output out_2
);

  or or_1 (out_2, in_1[0], in_1[1], in_1[2], in_1[3], in_1[5], in_1[6], in_1[7], in_1[4]);
endmodule

module _4_bit_counter (
  input  in_1,
  input  r,
  output out_3,
  output out_4,
  output out_5,
  output out_6
);

  wire and_1_out, bit_memory_1_out_5, bit_memory_2_out_5, bit_memory_3_out_5, not_1_out, not_2_out,
       not_3_out, not_4_out, not_5_out, not_6_out, or_1_out;

  or or_1 (or_1_out, r, bit_memory_3_out_5);
  bit_memory bit_memory_1 (
    .in_2(bit_memory_2_out_5), .in_3(or_1_out), .out_5(bit_memory_1_out_5), .in_1(1'b1),
    .in_4(bit_memory_2_out_5));
  not not_1 (not_1_out, in_1);
  bit_memory bit_memory_2 (.in_2(in_1), .in_3(or_1_out), .out_5(bit_memory_2_out_5), .in_1(not_1_out), .in_4(in_1));
  not not_2 (not_2_out, in_1);
  bit_memory bit_memory_3 (
    .in_2(and_1_out), .in_3(in_1), .out_5(bit_memory_3_out_5), .in_1(not_2_out), .in_4(and_1_out));
  and and_1 (and_1_out, bit_memory_1_out_5, in_1);
  and and_2 (out_3, in_1, bit_memory_1_out_5);
  not not_3 (not_3_out, in_1);
  and and_3 (out_4, not_3_out, bit_memory_1_out_5);
  and and_4 (out_5, in_1, not_4_out);
  not not_4 (not_4_out, bit_memory_1_out_5);
  not not_5 (not_5_out, in_1);
  and and_5 (out_6, not_5_out, not_6_out);
  not not_6 (not_6_out, bit_memory_1_out_5);
endmodule

module computer (
  input  power,
  input  in_2,
  input  [7:0] in_3,
  input  [7:0] in_4,
  input  \initial ,
  input  [7:0] in_6,
  input  in_7,
  input  [7:0] my_code,
  input  [7:0] in_9,
  output [7:0] out_10
);

  wire add_1_out_5, and_1_out, byte_is_on_1_out_2, byte_is_on_2_out_2, clock_1_out,
       instruction_decoder_1_add_im1___im2____im3, instruction_decoder_1_reset_byte,
       instruction_decoder_1_reset_byte__im1, instruction_decoder_1_reset_im3,
       instruction_decoder_1_save_mem_byte__im3, instruction_decoder_1_store_byte__im1,
       n8_tick_delay_1_out_2, n8_tick_delay_2_out_2, not_1_out, not_2_out, not_3_out, not_4_out, not_5_out,
       not_6_out, not_7_out, or_1_out, or_2_out, or_3_out, or_4_out;
  wire [7:0] add_1_out_4, address1_out, byte_1_out, byte_path_1_out_3, byte_path_2_out_3, byte_path_3_out_3,
       byte_path_4_out_3, byte_path_5_out_3, byte_path_6_out_3, byte_path_7_out_3, IM2_out, IM3_out,
       instruction_decoder_1_next_instruction__xxx, Instruction_Memory_1_out, main_memory_byte_output,
       n2_byte_stream_converge_1_out_3, n2_byte_stream_converge_2_out_3, n2_byte_stream_converge_3_out_3,
       n2_byte_stream_converge_4_out_3, n2_byte_stream_converge_5_out_3, next_instruction_out,
       read_mem_out_3, reset_byte_out_3;

  Clock clock_1 (.out(clock_1_out));
  _8_tick_delay u_8_tick_delay_1 (.in_1(instruction_decoder_1_store_byte__im1), .out_2(n8_tick_delay_1_out_2));
  _8_tick_delay u_8_tick_delay_2 (.in_1(n8_tick_delay_1_out_2), .out_2(n8_tick_delay_2_out_2));
  byte_path byte_path_1 (
    .location(Instruction_Memory_1_out), .pass(instruction_decoder_1_add_im1___im2____im3),
    .out_3(byte_path_1_out_3));
  byte_path byte_path_2 (
    .location(IM2_out), .pass(instruction_decoder_1_add_im1___im2____im3), .out_3(byte_path_2_out_3));
  not not_1 (not_1_out, clock_1_out);
  or or_1 (or_1_out, power, clock_1_out);
  add add_1 (
    .in_1(byte_path_1_out_3), .in_2(byte_path_2_out_3), .in_3(power), .out_4(add_1_out_4), .out_5(add_1_out_5));
  \byte  next_instruction (
    .in(n2_byte_stream_converge_1_out_3), .store(not_1_out), .out(next_instruction_out), .read(clock_1_out),
    .reset(not_2_out));
  not not_2 (not_2_out, not_3_out);
  not not_3 (not_3_out, not_4_out);
  not not_4 (not_4_out, not_5_out);
  not not_5 (not_5_out, or_1_out);
  _2_byte_stream_converge u_2_byte_stream_converge_1 (
    .in_1(byte_path_3_out_3), .in_2(byte_path_5_out_3), .out_3(n2_byte_stream_converge_1_out_3));
  byte_path byte_path_3 (.location(in_3), .pass(in_2), .out_3(byte_path_3_out_3));
  \byte  address1 (.in(in_4), .store(\initial ), .out(address1_out), .read(clock_1_out), .reset(power));
  \byte  Instruction_Memory_1 (
    .in(main_memory_byte_output), .store(n8_tick_delay_2_out_2), .out(Instruction_Memory_1_out),
    .read(instruction_decoder_1_add_im1___im2____im3), .reset(or_2_out));
  or or_2 (or_2_out, power, instruction_decoder_1_reset_byte__im1);
  \byte  IM2 (.in(in_6), .store(in_7), .out(IM2_out), .read(instruction_decoder_1_add_im1___im2____im3), .reset(power));
  \byte  IM3 (
    .in(add_1_out_4), .store(add_1_out_5), .out(IM3_out), .read(instruction_decoder_1_save_mem_byte__im3),
    .reset(or_3_out));
  or or_3 (or_3_out, power, instruction_decoder_1_reset_im3);
  not not_6 (not_6_out, not_1_out);
  not not_7 (not_7_out, not_6_out);
  \byte  byte_1 (
    .in(instruction_decoder_1_next_instruction__xxx), .store(and_1_out), .out(byte_1_out), .read(not_1_out),
    .reset(not_7_out));
  byte_path byte_path_4 (.location(next_instruction_out), .pass(not_2_out), .out_3(byte_path_4_out_3));
  and and_1 (and_1_out, or_1_out, byte_is_on_1_out_2);
  byte_is_on byte_is_on_1 (.in_1(instruction_decoder_1_next_instruction__xxx), .out_2(byte_is_on_1_out_2));
  byte_path byte_path_5 (.location(main_memory_byte_output), .pass(not_1_out), .out_3(byte_path_5_out_3));
  \byte  temp_display (
    .in(IM3_out), .store(byte_is_on_2_out_2), .out(out_10), .read(1'b1),
    .reset(instruction_decoder_1_reset_byte));
  byte_is_on byte_is_on_2 (.in_1(IM3_out), .out_2(byte_is_on_2_out_2));
  instruction_decoder instruction_decoder_1 (
    .in_1(byte_path_4_out_3), .next_instruction__xxx(instruction_decoder_1_next_instruction__xxx),
    .reset_byte(instruction_decoder_1_reset_byte), .reset_byte__IM1(instruction_decoder_1_reset_byte__im1),
    .store_byte__IM1(instruction_decoder_1_store_byte__im1),
    .save_mem_byte__IM3(instruction_decoder_1_save_mem_byte__im3),
    .add_IM1___IM2____IM3(instruction_decoder_1_add_im1___im2____im3),
    .reset_IM3(instruction_decoder_1_reset_im3));  // open: reset_byte__Address, store_byte__Address, save_mem_byte__Address, save_mem_byte__IM1, IM1____IM2, sub_IM1___IM2____IM3, IM1___IM2____IM3, IM1___IM2____IM3_2, IM1___IM2____IM3_3
  buf or_4 (or_4_out, instruction_decoder_1_save_mem_byte__im3);  // OR_Gate
  byte_path byte_path_6 (.location(address1_out), .pass(or_4_out), .out_3(byte_path_6_out_3));
  byte_path reset_byte (.location(address1_out), .pass(instruction_decoder_1_reset_byte), .out_3(reset_byte_out_3));
  byte_path read_mem (.location(address1_out), .pass(instruction_decoder_1_store_byte__im1), .out_3(read_mem_out_3));
  _2_byte_stream_converge u_2_byte_stream_converge_2 (
    .in_1(byte_1_out), .in_2(read_mem_out_3), .out_3(n2_byte_stream_converge_2_out_3));
  _2_byte_stream_converge u_2_byte_stream_converge_3 (
    .in_1(in_9), .in_2(IM3_out), .out_3(n2_byte_stream_converge_3_out_3));
  _8_byte_memory main_memory (
    .byte_input(n2_byte_stream_converge_3_out_3), .store(n2_byte_stream_converge_4_out_3),
    .read(n2_byte_stream_converge_2_out_3), .reset(n2_byte_stream_converge_5_out_3),
    .byte_output(main_memory_byte_output));
  _2_byte_stream_converge u_2_byte_stream_converge_4 (
    .in_1(byte_path_6_out_3), .in_2(my_code), .out_3(n2_byte_stream_converge_4_out_3));
  _2_byte_stream_converge u_2_byte_stream_converge_5 (
    .in_1(reset_byte_out_3), .in_2(byte_path_7_out_3), .out_3(n2_byte_stream_converge_5_out_3));
  byte_path byte_path_7 (.location({8{1'b1}}), .pass(power), .out_3(byte_path_7_out_3));
endmodule

module _8_bit_counter (
  input  in_1,
  input  in_2,
  output out_3,
  output out_4,
  output out_5,
  output out_6,
  output out_7,
  output out_8,
  output out_9,
  output out_10
);

  wire and_2_out, n4_bit_counter_1_out_3, n4_bit_counter_1_out_4, n4_bit_counter_1_out_5,
       n4_bit_counter_1_out_6, n4_bit_counter_2_out_3, n4_bit_counter_2_out_4, n4_bit_counter_2_out_5,
       n4_bit_counter_2_out_6, not_1_out, or_1_out;

  // AND_Gate and_1 has open pins: in0=in_1, in1=n4_bit_counter_1_out_4, out=open
  and and_2 (and_2_out, n4_bit_counter_1_out_3, in_1);
  _4_bit_counter u_4_bit_counter_1 (
    .in_1(in_1), .r(in_2), .out_3(n4_bit_counter_1_out_3), .out_4(n4_bit_counter_1_out_4),
    .out_5(n4_bit_counter_1_out_5), .out_6(n4_bit_counter_1_out_6));
  buf or_1 (or_1_out, and_2_out);  // OR_Gate
  _4_bit_counter u_4_bit_counter_2 (
    .in_1(or_1_out), .r(in_2), .out_3(n4_bit_counter_2_out_3), .out_4(n4_bit_counter_2_out_4),
    .out_5(n4_bit_counter_2_out_5), .out_6(n4_bit_counter_2_out_6));
  and and_3 (out_3, n4_bit_counter_2_out_3, n4_bit_counter_1_out_3);
  and and_4 (out_4, n4_bit_counter_2_out_4, n4_bit_counter_1_out_4);
  and and_5 (out_5, n4_bit_counter_2_out_4, n4_bit_counter_1_out_5);
  not not_1 (not_1_out, n4_bit_counter_2_out_6);
  and and_6 (out_6, not_1_out, n4_bit_counter_1_out_6);
  and and_7 (out_7, n4_bit_counter_2_out_5, n4_bit_counter_1_out_3);
  and and_8 (out_8, n4_bit_counter_2_out_6, n4_bit_counter_1_out_4);
  and and_9 (out_9, n4_bit_counter_2_out_6, n4_bit_counter_1_out_5);
  and and_10 (out_10, n4_bit_counter_2_out_6, n4_bit_counter_1_out_6);
endmodule

module byte_delay (
  input  [7:0] in_1,
  output [7:0] out_2
);

  wire not_2_out, not_4_out, not_6_out, not_8_out, not_9_out, not_11_out, not_14_out, not_16_out;

  not not_1 (out_2[0], not_2_out);
  not not_2 (not_2_out, in_1[0]);
  not not_3 (out_2[1], not_4_out);
  not not_4 (not_4_out, in_1[1]);
  not not_5 (out_2[2], not_6_out);
  not not_6 (not_6_out, in_1[2]);
  not not_7 (out_2[3], not_8_out);
  not not_8 (not_8_out, in_1[3]);
  not not_9 (not_9_out, in_1[4]);
  not not_10 (out_2[4], not_9_out);
  not not_11 (not_11_out, in_1[5]);
  not not_12 (out_2[5], not_11_out);
  not not_13 (out_2[6], not_14_out);
  not not_14 (not_14_out, in_1[6]);
  not not_15 (out_2[7], not_16_out);
  not not_16 (not_16_out, in_1[7]);
endmodule

module _1_tick_delay (
  input  in_1,
  output out_2
);

  buf or_1 (out_2, in_1);  // OR_Gate
endmodule

module _1_tick_extender (
  input  in_1,
  output out_2
);

  wire not_1_out, not_2_out;

  not not_1 (not_1_out, not_2_out);
  not not_2 (not_2_out, in_1);
  or or_1 (out_2, not_1_out, in_1);
endmodule

module _1_tick_byte_extender (
  input  [7:0] in_1,
  output [7:0] out_2
);

  _1_tick_extender u_1_tick_extender_1 (.in_1(in_1[0]), .out_2(out_2[0]));
  _1_tick_extender u_1_tick_extender_2 (.in_1(in_1[1]), .out_2(out_2[1]));
  _1_tick_extender u_1_tick_extender_3 (.in_1(in_1[2]), .out_2(out_2[2]));
  _1_tick_extender u_1_tick_extender_4 (.in_1(in_1[3]), .out_2(out_2[3]));
  _1_tick_extender u_1_tick_extender_5 (.in_1(in_1[4]), .out_2(out_2[4]));
  _1_tick_extender u_1_tick_extender_6 (.in_1(in_1[5]), .out_2(out_2[5]));
  _1_tick_extender u_1_tick_extender_7 (.in_1(in_1[6]), .out_2(out_2[6]));
  _1_tick_extender u_1_tick_extender_8 (.in_1(in_1[7]), .out_2(out_2[7]));
endmodule

module _2_tick_delay (
  input  in_1,
  output out_2
);


  assign out_2 = in_1;
endmodule

module _8_tick_delay (
  input  in_1,
  output out_2
);

  wire or_1_out, or_2_out, or_3_out, or_4_out, or_5_out, or_6_out, or_7_out;

  buf or_1 (or_1_out, in_1);  // OR_Gate
  buf or_2 (or_2_out, or_1_out);  // OR_Gate
  buf or_3 (or_3_out, or_2_out);  // OR_Gate
  buf or_4 (or_4_out, or_3_out);  // OR_Gate
  buf or_5 (or_5_out, or_6_out);  // OR_Gate
  buf or_6 (or_6_out, or_4_out);  // OR_Gate
  buf or_7 (or_7_out, or_5_out);  // OR_Gate
  buf or_8 (out_2, or_7_out);  // OR_Gate
endmodule

module add (
  input  [7:0] in_1,
  input  [7:0] in_2,
  input  in_3,
  output [7:0] out_4,
  output out_5
);

  wire byte_is_on_1_out_2, n1_tick_delay_1_out_2, n1_tick_extender_1_out_2, n1_tick_extender_2_out_2,
       n1_tick_extender_3_out_2, n1_tick_extender_4_out_2, n1_tick_extender_5_out_2, n8_tick_delay_1_out_2,
       n8_tick_delay_2_out_2, n8_tick_delay_3_out_2, n8_tick_delay_4_out_2, n8_tick_delay_5_out_2,
       n8_tick_delay_6_out_2, n8_tick_delay_7_out_2, n8_tick_delay_8_out_2, or_1_out;
  wire [7:0] byte_1_out, byte_2_out, byte_path_1_out_3, n1_tick_byte_extender_1_out_2,
       n1_tick_byte_extender_2_out_2, n1_tick_byte_extender_3_out_2, n1_tick_byte_extender_4_out_2,
       n2_byte_stream_converge_1_out_3, undriven, undriven_2;
  wire [15:0] addition_1_out_5;

  _1_tick_byte_extender u_1_tick_byte_extender_1 (.in_1(in_1), .out_2(n1_tick_byte_extender_1_out_2));
  _1_tick_byte_extender u_1_tick_byte_extender_2 (.in_1(in_2), .out_2(n1_tick_byte_extender_2_out_2));
  _1_tick_byte_extender u_1_tick_byte_extender_3 (
    .in_1(n1_tick_byte_extender_1_out_2), .out_2(n1_tick_byte_extender_3_out_2));
  \byte  byte_1 (
    .in(n1_tick_byte_extender_3_out_2), .store(n1_tick_extender_1_out_2), .out(byte_1_out), .read(1'b1),
    .reset(or_1_out));
  _1_tick_byte_extender u_1_tick_byte_extender_4 (
    .in_1(n1_tick_byte_extender_2_out_2), .out_2(n1_tick_byte_extender_4_out_2));
  \byte  byte_2 (
    .in(n1_tick_byte_extender_4_out_2), .store(n1_tick_extender_1_out_2), .out(byte_2_out), .read(1'b1),
    .reset(or_1_out));
  _1_tick_extender u_1_tick_extender_1 (.in_1(byte_is_on_1_out_2), .out_2(n1_tick_extender_1_out_2));
  _2_byte_stream_converge u_2_byte_stream_converge_1 (
    .in_1(in_2), .in_2(in_1), .out_3(n2_byte_stream_converge_1_out_3));
  or or_1 (or_1_out, n1_tick_extender_2_out_2, n1_tick_extender_4_out_2, in_3);
  byte_is_on byte_is_on_1 (.in_1(n2_byte_stream_converge_1_out_3), .out_2(byte_is_on_1_out_2));
  _1_tick_extender u_1_tick_extender_2 (.in_1(n1_tick_extender_3_out_2), .out_2(n1_tick_extender_2_out_2));
  _8_tick_delay u_8_tick_delay_1 (.in_1(byte_is_on_1_out_2), .out_2(n8_tick_delay_1_out_2));
  _8_tick_delay u_8_tick_delay_2 (.in_1(n8_tick_delay_1_out_2), .out_2(n8_tick_delay_2_out_2));
  _1_tick_extender u_1_tick_extender_3 (.in_1(n8_tick_delay_8_out_2), .out_2(n1_tick_extender_3_out_2));
  _1_tick_extender u_1_tick_extender_4 (.in_1(n8_tick_delay_8_out_2), .out_2(n1_tick_extender_4_out_2));
  _8_tick_delay u_8_tick_delay_3 (.in_1(n8_tick_delay_4_out_2), .out_2(n8_tick_delay_3_out_2));
  _8_tick_delay u_8_tick_delay_4 (.in_1(n8_tick_delay_5_out_2), .out_2(n8_tick_delay_4_out_2));
  _8_tick_delay u_8_tick_delay_5 (.in_1(n8_tick_delay_2_out_2), .out_2(n8_tick_delay_5_out_2));
  addition addition_1 (
    .in_1({undriven, byte_1_out}), .in_2({undriven_2, byte_2_out}), .in_3(1'b0), .out_5(addition_1_out_5));  // open: out_4
  _8_tick_delay u_8_tick_delay_6 (.in_1(n8_tick_delay_7_out_2), .out_2(n8_tick_delay_6_out_2));
  _8_tick_delay u_8_tick_delay_7 (.in_1(n8_tick_delay_3_out_2), .out_2(n8_tick_delay_7_out_2));
  _8_tick_delay u_8_tick_delay_8 (.in_1(n8_tick_delay_6_out_2), .out_2(n8_tick_delay_8_out_2));
  byte_path byte_path_1 (.location(addition_1_out_5[7:0]), .pass(n8_tick_delay_6_out_2), .out_3(byte_path_1_out_3));
  _1_tick_byte_extender u_1_tick_byte_extender_5 (.in_1(byte_path_1_out_3), .out_2(out_4));
  _1_tick_extender u_1_tick_extender_5 (.in_1(n1_tick_delay_1_out_2), .out_2(n1_tick_extender_5_out_2));
  _1_tick_delay u_1_tick_delay_1 (.in_1(n8_tick_delay_6_out_2), .out_2(n1_tick_delay_1_out_2));
  _1_tick_extender u_1_tick_extender_6 (.in_1(n1_tick_extender_5_out_2), .out_2(out_5));
endmodule
