// Logisim project testing clocks.circ as structural Verilog: 1 circuit, main circuit main
module main (
  input  in_1,
  input  in_2,
  input  in_3,
  input  in_4,
  input  in_5,
  input  in_6,
  input  in_7,
  input  [6:0] in_8
);

  wire clock_1_out, counter_1_out_3, counter_1_out_4, counter_2_out_3, counter_2_out_4, counter_3_out_3,
       counter_3_out_4, counter_4_out_3, counter_4_out_4, counter_5_out_3, counter_5_out_4, counter_6_out_3,
       counter_6_out_4, counter_7_out_4, keyboard_1_avail;
  wire [6:0] keyboard_1_data;

  Clock clock_1 (.out(clock_1_out));
  counter counter_1 (.store(counter_2_out_3), .reset(in_7), .out_3(counter_1_out_3), .out_4(counter_1_out_4));
  counter counter_2 (.store(clock_1_out), .reset(in_7), .out_3(counter_2_out_3), .out_4(counter_2_out_4));
  Keyboard keyboard_1 (.clk(in_1), .re(in_3), .clr(in_5), .avail(keyboard_1_avail), .data(keyboard_1_data));
  counter counter_3 (.store(counter_1_out_3), .reset(in_7), .out_3(counter_3_out_3), .out_4(counter_3_out_4));
  counter counter_4 (.store(counter_3_out_3), .reset(in_7), .out_3(counter_4_out_3), .out_4(counter_4_out_4));
  counter counter_5 (.store(counter_4_out_3), .reset(in_7), .out_3(counter_5_out_3), .out_4(counter_5_out_4));
  counter counter_6 (.store(counter_5_out_3), .reset(in_7), .out_3(counter_6_out_3), .out_4(counter_6_out_4));
  counter counter_7 (.store(counter_6_out_3), .reset(in_7), .out_4(counter_7_out_4));  // open: out_3
  TTY tty_1 (.data(keyboard_1_data), .clk(in_1), .we(in_4), .clr(in_6));
  DotMatrix dotmatrix_1 (.col0(in_8));  // open: col1, col2, col3, col4
endmodule
