// Logisim project testing.circ as structural Verilog: 26 circuits, main circuit main
module main (
  output [15:0] out_1,
  output [15:0] out_2,
  output [15:0] out_3
);

  wire _4_bit_out_2, and_1_out, and_2_out, and_3_out, and_4_out, and_5_out, and_6_out, and_7_out,
       bit_storage_1_out_3, bit_storage_2_out_3, bit_storage_3_out_3, bit_storage_4_out_3,
       bit_storage_5_out_3, button_2_out, button_3_out, button_4_out, button_out, C_out, counter_1_out_3,
       counter_1_out_4, not_1_out, not_2_out, or_1_out, x_out;
  wire [2:0] base10_to_display_17_out_2_2, base10_to_display_18_out_2_2;
  wire [3:0] _4_bit_out_3, base10_to_display_17_out_2, base10_to_display_18_out_2, input_number_1_out_4,
       input_number_1_out_5, input_number_1_out_6, input_number_1_out_7, input_number_1_out_8,
       input_number_2_out_4, input_number_2_out_5, input_number_2_out_6, input_number_2_out_7,
       input_number_2_out_8, n4_bit_gateway_1_out_3, n4_bit_gateway_2_out_3;
  wire [6:0] base10_to_display_1_out_2, base10_to_display_2_out_2, base10_to_display_3_out_2,
       base10_to_display_4_out_2, base10_to_display_5_out_2, base10_to_display_6_out_2,
       base10_to_display_7_out_2, base10_to_display_8_out_2, base10_to_display_9_out_2,
       base10_to_display_10_out_2, base10_to_display_11_out_2, base10_to_display_12_out_2,
       base10_to_display_13_out_2, base10_to_display_14_out_2, base10_to_display_15_out_2,
       base10_to_display_16_out_2;
  wire [9:0] _0_out, n4_bit_to_base10_1_out_2, n4_bit_to_base10_2_out_2, n4_bit_to_base10_3_out_2,
       n4_bit_to_base10_4_out_2, n4_bit_to_base10_5_out_2, n4_bit_to_base10_6_out_2,
       n4_bit_to_base10_7_out_2, n4_bit_to_base10_8_out_2, n4_bit_to_base10_9_out_2,
       n4_bit_to_base10_10_out_2, n4_bit_to_base10_11_out_2, n4_bit_to_base10_12_out_2,
       n4_bit_to_base10_13_out_2, n4_bit_to_base10_14_out_2, n4_bit_to_base10_15_out_2,
       n4_bit_to_base10_16_out_2, n4_bit_to_base10_17_out_2, n4_bit_to_base10_18_out_2;
  wire [15:0] addition_1_out_3, addition_2_out_3, multiplication_1_out_3, n16_bit_gateway_1_out_3,
       n16_bit_gateway_2_out_3, n16_bit_gateway_3_out_3, n16_bit_gateway_4_out_3, n16_bit_gateway_5_out_3,
       n16_bit_gateway_6_out_3, subtraction_1_out_3;

  Button _1 (.out(_0_out[1]));
  Button _2 (.out(_0_out[2]));
  Button _3 (.out(_0_out[3]));
  Button _4 (.out(_0_out[4]));
  Button _5 (.out(_0_out[5]));
  Button _6 (.out(_0_out[6]));
  Button _7 (.out(_0_out[7]));
  Button _8 (.out(_0_out[8]));
  Button _9 (.out(_0_out[9]));
  Button _0 (.out(_0_out[0]));
  Button C (.out(C_out));
  Button button (.out(button_out));
  Button button_2 (.out(button_2_out));
  Button button_3 (.out(button_3_out));
  Button x (.out(x_out));
  input_to_binary input_to_binary_1 (
    .in_1({input_number_1_out_8, input_number_1_out_7, input_number_1_out_6, input_number_1_out_5, input_number_1_out_4}),
    .out_2(out_1));
  input_to_binary input_to_binary_2 (
    .in_1({input_number_2_out_8, input_number_2_out_7, input_number_2_out_6, input_number_2_out_5, input_number_2_out_4}),
    .out_2(out_2));
  _16_bit_gateway u_16_bit_gateway_1 (.in_1(out_1), .in_2(and_4_out), .out_3(n16_bit_gateway_1_out_3));
  _16_bit_gateway u_16_bit_gateway_2 (.in_1(out_2), .in_2(and_4_out), .out_3(n16_bit_gateway_2_out_3));
  _16_bit_gateway u_16_bit_gateway_3 (.in_1(out_1), .in_2(and_5_out), .out_3(n16_bit_gateway_3_out_3));
  _16_bit_gateway u_16_bit_gateway_4 (.in_1(out_2), .in_2(and_5_out), .out_3(n16_bit_gateway_4_out_3));
  _16_bit_gateway u_16_bit_gateway_5 (.in_1(out_1), .in_2(and_6_out), .out_3(n16_bit_gateway_5_out_3));
  _16_bit_gateway u_16_bit_gateway_6 (.in_1(out_2), .in_2(and_6_out), .out_3(n16_bit_gateway_6_out_3));
  Button button_4 (.out(button_4_out));
  addition addition_1 (.in_1(n16_bit_gateway_1_out_3), .in_2(n16_bit_gateway_2_out_3), .out_3(addition_1_out_3));
  subtraction subtraction_1 (
    .in_1(n16_bit_gateway_3_out_3), .in_2(n16_bit_gateway_4_out_3), .out_3(subtraction_1_out_3));
  multiplication multiplication_1 (
    .in_1(n16_bit_gateway_5_out_3), .in_2(n16_bit_gateway_6_out_3), .out_3(multiplication_1_out_3));
  addition addition_2 (.in_1(addition_1_out_3), .in_2(subtraction_1_out_3), .out_3(addition_2_out_3));
  base10_to_4_bit _4_bit (.in_1(_0_out), .out_2(_4_bit_out_2), .out_3(_4_bit_out_3));
  and and_1 (and_1_out, not_2_out, not_1_out);
  not not_1 (not_1_out, counter_1_out_4);
  not not_2 (not_2_out, counter_1_out_3);
  counter counter_1 (.store(or_1_out), .reset(C_out), .out_3(counter_1_out_3), .out_4(counter_1_out_4));
  or or_1 (or_1_out, button_out, button_2_out, button_4_out, x_out, button_3_out);
  bit_storage bit_storage_1 (.store(button_4_out), .reset(C_out), .out_3(bit_storage_1_out_3));
  bit_storage bit_storage_2 (.store(button_out), .reset(C_out), .out_3(bit_storage_2_out_3));
  bit_storage bit_storage_3 (.store(button_2_out), .reset(C_out), .out_3(bit_storage_3_out_3));
  bit_storage bit_storage_4 (.store(x_out), .reset(C_out), .out_3(bit_storage_4_out_3));
  bit_storage bit_storage_5 (.store(button_3_out), .reset(C_out), .out_3(bit_storage_5_out_3));
  addition addition_3 (.in_1(addition_2_out_3), .in_2(multiplication_1_out_3), .out_3(out_3));
  and and_2 (and_2_out, _4_bit_out_2, and_1_out);
  input_number input_number_1 (
    .in(n4_bit_gateway_1_out_3), .r(C_out), .counter(and_2_out), .out_4(input_number_1_out_4),
    .out_5(input_number_1_out_5), .out_6(input_number_1_out_6), .out_7(input_number_1_out_7),
    .out_8(input_number_1_out_8));
  _4_bit_gateway u_4_bit_gateway_1 (.in_1(_4_bit_out_3), .in_2(and_1_out), .out_3(n4_bit_gateway_1_out_3));
  and and_3 (and_3_out, _4_bit_out_2, counter_1_out_4);
  input_number input_number_2 (
    .in(n4_bit_gateway_2_out_3), .r(C_out), .counter(and_3_out), .out_4(input_number_2_out_4),
    .out_5(input_number_2_out_5), .out_6(input_number_2_out_6), .out_7(input_number_2_out_7),
    .out_8(input_number_2_out_8));
  _4_bit_gateway u_4_bit_gateway_2 (.in_1(_4_bit_out_3), .in_2(counter_1_out_4), .out_3(n4_bit_gateway_2_out_3));
  and and_4 (and_4_out, bit_storage_2_out_3, bit_storage_1_out_3);
  and and_5 (and_5_out, bit_storage_3_out_3, bit_storage_1_out_3);
  and and_6 (and_6_out, bit_storage_4_out_3, bit_storage_1_out_3);
  and and_7 (and_7_out, bit_storage_5_out_3, bit_storage_1_out_3);
  _4_bit_to_base10 u_4_bit_to_base10_1 (.in_1(input_number_1_out_4), .out_2(n4_bit_to_base10_1_out_2));
  base10_to_display base10_to_display_1 (.in_1(n4_bit_to_base10_1_out_2), .out_2(base10_to_display_1_out_2));
  _4_bit_to_base10 u_4_bit_to_base10_2 (.in_1(input_number_1_out_5), .out_2(n4_bit_to_base10_2_out_2));
  base10_to_display base10_to_display_2 (.in_1(n4_bit_to_base10_2_out_2), .out_2(base10_to_display_2_out_2));
  _4_bit_to_base10 u_4_bit_to_base10_3 (.in_1(input_number_1_out_6), .out_2(n4_bit_to_base10_3_out_2));
  base10_to_display base10_to_display_3 (.in_1(n4_bit_to_base10_3_out_2), .out_2(base10_to_display_3_out_2));
  _4_bit_to_base10 u_4_bit_to_base10_4 (.in_1(input_number_1_out_7), .out_2(n4_bit_to_base10_4_out_2));
  _4_bit_to_base10 u_4_bit_to_base10_5 (.in_1(input_number_1_out_8), .out_2(n4_bit_to_base10_5_out_2));
  _4_bit_to_base10 u_4_bit_to_base10_6 (.in_1(input_number_2_out_4), .out_2(n4_bit_to_base10_6_out_2));
  base10_to_display base10_to_display_4 (.in_1(n4_bit_to_base10_6_out_2), .out_2(base10_to_display_4_out_2));
  _4_bit_to_base10 u_4_bit_to_base10_7 (.in_1(input_number_2_out_5), .out_2(n4_bit_to_base10_7_out_2));
  base10_to_display base10_to_display_5 (.in_1(n4_bit_to_base10_7_out_2), .out_2(base10_to_display_5_out_2));
  _4_bit_to_base10 u_4_bit_to_base10_8 (.in_1(input_number_2_out_6), .out_2(n4_bit_to_base10_8_out_2));
  base10_to_display base10_to_display_6 (.in_1(n4_bit_to_base10_8_out_2), .out_2(base10_to_display_6_out_2));
  _4_bit_to_base10 u_4_bit_to_base10_9 (.in_1(input_number_2_out_7), .out_2(n4_bit_to_base10_9_out_2));
  _4_bit_to_base10 u_4_bit_to_base10_10 (.in_1(input_number_2_out_8), .out_2(n4_bit_to_base10_10_out_2));
  _4_bit_to_base10 u_4_bit_to_base10_11 (.out_2(n4_bit_to_base10_11_out_2));  // open: in_1
  base10_to_display base10_to_display_7 (.in_1(n4_bit_to_base10_11_out_2), .out_2(base10_to_display_7_out_2));
  base10_to_display base10_to_display_8 (.in_1(n4_bit_to_base10_12_out_2), .out_2(base10_to_display_8_out_2));
  _4_bit_to_base10 u_4_bit_to_base10_12 (.out_2(n4_bit_to_base10_12_out_2));  // open: in_1
  base10_to_display base10_to_display_9 (.in_1(n4_bit_to_base10_13_out_2), .out_2(base10_to_display_9_out_2));
  _4_bit_to_base10 u_4_bit_to_base10_13 (.out_2(n4_bit_to_base10_13_out_2));  // open: in_1
  _4_bit_to_base10 u_4_bit_to_base10_14 (.out_2(n4_bit_to_base10_14_out_2));  // open: in_1
  base10_to_display base10_to_display_10 (.in_1(n4_bit_to_base10_14_out_2), .out_2(base10_to_display_10_out_2));
  _4_bit_to_base10 u_4_bit_to_base10_15 (.out_2(n4_bit_to_base10_15_out_2));  // open: in_1
  _4_bit_to_base10 u_4_bit_to_base10_16 (.out_2(n4_bit_to_base10_16_out_2));  // open: in_1
  _4_bit_to_base10 u_4_bit_to_base10_17 (.out_2(n4_bit_to_base10_17_out_2));  // open: in_1
  base10_to_display base10_to_display_11 (.in_1(n4_bit_to_base10_4_out_2), .out_2(base10_to_display_11_out_2));
  base10_to_display base10_to_display_12 (.in_1(n4_bit_to_base10_5_out_2), .out_2(base10_to_display_12_out_2));
  base10_to_display base10_to_display_13 (.in_1(n4_bit_to_base10_9_out_2), .out_2(base10_to_display_13_out_2));
  base10_to_display base10_to_display_14 (.in_1(n4_bit_to_base10_10_out_2), .out_2(base10_to_display_14_out_2));
  base10_to_display base10_to_display_15 (.in_1(n4_bit_to_base10_15_out_2), .out_2(base10_to_display_15_out_2));
  base10_to_display base10_to_display_16 (.in_1(n4_bit_to_base10_16_out_2), .out_2(base10_to_display_16_out_2));
  base10_to_display base10_to_display_17 (
    .in_1(n4_bit_to_base10_17_out_2), .out_2({base10_to_display_17_out_2_2, base10_to_display_17_out_2}));
  base10_to_display base10_to_display_18 (
    .in_1(n4_bit_to_base10_18_out_2), .out_2({base10_to_display_18_out_2_2, base10_to_display_18_out_2}));
  _4_bit_to_base10 u_4_bit_to_base10_18 (.out_2(n4_bit_to_base10_18_out_2));  // open: in_1
  _7_Segment_Display u_7_segment_display_1 (
    .g(base10_to_display_1_out_2[3]), .f(base10_to_display_1_out_2[2]), .a(base10_to_display_1_out_2[1]),
    .b(base10_to_display_1_out_2[0]), .e(base10_to_display_1_out_2[4]), .d(base10_to_display_1_out_2[5]),
    .c(base10_to_display_1_out_2[6]));  // open: dp
  _7_Segment_Display u_7_segment_display_2 (
    .g(base10_to_display_2_out_2[3]), .f(base10_to_display_2_out_2[2]), .a(base10_to_display_2_out_2[1]),
    .b(base10_to_display_2_out_2[0]), .e(base10_to_display_2_out_2[4]), .d(base10_to_display_2_out_2[5]),
    .c(base10_to_display_2_out_2[6]));  // open: dp
  _7_Segment_Display u_7_segment_display_3 (
    .g(base10_to_display_5_out_2[3]), .f(base10_to_display_5_out_2[2]), .a(base10_to_display_5_out_2[1]),
    .b(base10_to_display_5_out_2[0]), .e(base10_to_display_5_out_2[4]), .d(base10_to_display_5_out_2[5]),
    .c(base10_to_display_5_out_2[6]));  // open: dp
  _7_Segment_Display u_7_segment_display_4 (
    .g(base10_to_display_4_out_2[3]), .f(base10_to_display_4_out_2[2]), .a(base10_to_display_4_out_2[1]),
    .b(base10_to_display_4_out_2[0]), .e(base10_to_display_4_out_2[4]), .d(base10_to_display_4_out_2[5]),
    .c(base10_to_display_4_out_2[6]));  // open: dp
  _7_Segment_Display u_7_segment_display_5 (
    .g(base10_to_display_8_out_2[3]), .f(base10_to_display_8_out_2[2]), .a(base10_to_display_8_out_2[1]),
    .b(base10_to_display_8_out_2[0]), .e(base10_to_display_8_out_2[4]), .d(base10_to_display_8_out_2[5]),
    .c(base10_to_display_8_out_2[6]));  // open: dp
  _7_Segment_Display u_7_segment_display_6 (
    .g(base10_to_display_7_out_2[3]), .f(base10_to_display_7_out_2[2]), .a(base10_to_display_7_out_2[1]),
    .b(base10_to_display_7_out_2[0]), .e(base10_to_display_7_out_2[4]), .d(base10_to_display_7_out_2[5]),
    .c(base10_to_display_7_out_2[6]));  // open: dp
  _7_Segment_Display u_7_segment_display_7 (
    .g(base10_to_display_11_out_2[3]), .f(base10_to_display_11_out_2[2]), .a(base10_to_display_11_out_2[1]),
    .b(base10_to_display_11_out_2[0]), .e(base10_to_display_11_out_2[4]), .d(base10_to_display_11_out_2[5]),
    .c(base10_to_display_11_out_2[6]));  // open: dp
  _7_Segment_Display u_7_segment_display_8 (
    .g(base10_to_display_3_out_2[3]), .f(base10_to_display_3_out_2[2]), .a(base10_to_display_3_out_2[1]),
    .b(base10_to_display_3_out_2[0]), .e(base10_to_display_3_out_2[4]), .d(base10_to_display_3_out_2[5]),
    .c(base10_to_display_3_out_2[6]));  // open: dp
  _7_Segment_Display u_7_segment_display_9 (
    .g(base10_to_display_6_out_2[3]), .f(base10_to_display_6_out_2[2]), .a(base10_to_display_6_out_2[1]),
    .b(base10_to_display_6_out_2[0]), .e(base10_to_display_6_out_2[4]), .d(base10_to_display_6_out_2[5]),
    .c(base10_to_display_6_out_2[6]));  // open: dp
  _7_Segment_Display u_7_segment_display_10 (
    .g(base10_to_display_13_out_2[3]), .f(base10_to_display_13_out_2[2]), .a(base10_to_display_13_out_2[1]),
    .b(base10_to_display_13_out_2[0]), .e(base10_to_display_13_out_2[4]), .d(base10_to_display_13_out_2[5]),
    .c(base10_to_display_13_out_2[6]));  // open: dp
  _7_Segment_Display u_7_segment_display_11 (
    .g(base10_to_display_10_out_2[3]), .f(base10_to_display_10_out_2[2]), .a(base10_to_display_10_out_2[1]),
    .b(base10_to_display_10_out_2[0]), .e(base10_to_display_10_out_2[4]), .d(base10_to_display_10_out_2[5]),
    .c(base10_to_display_10_out_2[6]));  // open: dp
  _7_Segment_Display u_7_segment_display_12 (
    .g(base10_to_display_9_out_2[3]), .f(base10_to_display_9_out_2[2]), .a(base10_to_display_9_out_2[1]),
    .b(base10_to_display_9_out_2[0]), .e(base10_to_display_9_out_2[4]), .d(base10_to_display_9_out_2[5]),
    .c(base10_to_display_9_out_2[6]));  // open: dp
  _7_Segment_Display u_7_segment_display_13 (
    .g(base10_to_display_12_out_2[3]), .f(base10_to_display_12_out_2[2]), .a(base10_to_display_12_out_2[1]),
    .b(base10_to_display_12_out_2[0]), .e(base10_to_display_12_out_2[4]), .d(base10_to_display_12_out_2[5]),
    .c(base10_to_display_12_out_2[6]));  // open: dp
  _7_Segment_Display u_7_segment_display_14 (
    .g(base10_to_display_14_out_2[3]), .f(base10_to_display_14_out_2[2]), .a(base10_to_display_14_out_2[1]),
    .b(base10_to_display_14_out_2[0]), .e(base10_to_display_14_out_2[4]), .d(base10_to_display_14_out_2[5]),
    .c(base10_to_display_14_out_2[6]));  // open: dp
  _7_Segment_Display u_7_segment_display_15 (
    .g(base10_to_display_16_out_2[3]), .f(base10_to_display_16_out_2[2]), .a(base10_to_display_16_out_2[1]),
    .b(base10_to_display_16_out_2[0]), .e(base10_to_display_16_out_2[4]), .d(base10_to_display_16_out_2[5]),
    .c(base10_to_display_16_out_2[6]));  // open: dp
  _7_Segment_Display u_7_segment_display_16 (
    .g(base10_to_display_15_out_2[3]), .f(base10_to_display_15_out_2[2]), .a(base10_to_display_15_out_2[1]),
    .b(base10_to_display_15_out_2[0]), .e(base10_to_display_15_out_2[4]), .d(base10_to_display_15_out_2[5]),
    .c(base10_to_display_15_out_2[6]));  // open: dp
  _7_Segment_Display u_7_segment_display_17 (
    .g(base10_to_display_17_out_2[3]), .f(base10_to_display_17_out_2[2]), .a(base10_to_display_17_out_2[1]),
    .b(base10_to_display_17_out_2[0]), .e(base10_to_display_17_out_2_2[0]),
    .d(base10_to_display_17_out_2_2[1]), .c(base10_to_display_17_out_2_2[2]));  // open: dp
  _7_Segment_Display u_7_segment_display_18 (
    .g(base10_to_display_18_out_2[3]), .f(base10_to_display_18_out_2[2]), .a(base10_to_display_18_out_2[1]),
    .b(base10_to_display_18_out_2[0]), .e(base10_to_display_18_out_2_2[0]),
    .d(base10_to_display_18_out_2_2[1]), .c(base10_to_display_18_out_2_2[2]));  // open: dp
endmodule

module _1_bit_sum (
  input  in_1,
  input  in_2,
  input  in_3,
  output out_4,
  output out_5
);

  wire and_1_out, and_2_out, and_3_out, and_4_out, and_5_out, not_1_out, or_1_out;

  and and_1 (and_1_out, in_1, in_2);
  and and_2 (and_2_out, in_1, in_3);
  and and_3 (and_3_out, in_2, in_3);
  not not_1 (not_1_out, out_4);
  or or_1 (or_1_out, in_1, in_2, in_3);
  or or_2 (out_4, and_1_out, and_2_out, and_3_out);
  and and_4 (and_4_out, and_2_out, and_3_out);
  and and_5 (and_5_out, not_1_out, or_1_out);
  or or_3 (out_5, and_4_out, and_5_out);
endmodule

module _4_bit_sum (
  input  in_1,
  input  in_2,
  input  in_3,
  input  in_4,
  input  in_5,
  input  in_6,
  input  in_7,
  input  in_8,
  input  rin,
  output out_10,
  output out_11,
  output out_12,
  output out_13,
  output out_14
);

  wire n1_bit_sum_2_out_4, n1_bit_sum_3_out_4, n1_bit_sum_4_out_4;

  _1_bit_sum u_1_bit_sum_1 (.in_1(in_1), .in_2(in_5), .out_4(out_10), .in_3(n1_bit_sum_2_out_4), .out_5(out_11));
  _1_bit_sum u_1_bit_sum_2 (
    .in_1(in_2), .in_2(in_6), .out_4(n1_bit_sum_2_out_4), .in_3(n1_bit_sum_3_out_4), .out_5(out_12));
  _1_bit_sum u_1_bit_sum_3 (
    .in_1(in_3), .in_2(in_7), .out_4(n1_bit_sum_3_out_4), .in_3(n1_bit_sum_4_out_4), .out_5(out_13));
  _1_bit_sum u_1_bit_sum_4 (.in_1(in_4), .in_2(in_8), .out_4(n1_bit_sum_4_out_4), .in_3(rin), .out_5(out_14));
endmodule

module _16_bit_addition (
  input  in_1,
  input  in_2,
  input  in_3,
  input  in_4,
  input  in_5,
  input  in_6,
  input  in_7,
  input  in_8,
  input  in_9,
  input  in_10,
  input  in_11,
  input  in_12,
  input  in_13,
  input  in_14,
  input  in_15,
  input  in_16,
  input  in_17,
  input  in_18,
  input  in_19,
  input  in_20,
  input  in_21,
  input  in_22,
  input  in_23,
  input  in_24,
  input  in_25,
  input  in_26,
  input  in_27,
  input  in_28,
  input  in_29,
  input  in_30,
  input  in_31,
  input  in_32,
  output out_33,
  output out_34,
  output out_35,
  output out_36,
  output out_37,
  output out_38,
  output out_39,
  output out_40,
  output out_41,
  output out_42,
  output out_43,
  output out_44,
  output out_45,
  output out_46,
  output out_47,
  output out_48
);

  wire n4_bit_sum_2_out_10, n4_bit_sum_3_out_10, n4_bit_sum_4_out_10;

  _4_bit_sum u_4_bit_sum_1 (
    .in_1(in_1), .in_2(in_4), .in_3(in_7), .in_4(in_8), .in_5(in_2), .in_6(in_3), .in_7(in_5), .in_8(in_6),
    .rin(n4_bit_sum_2_out_10), .out_11(out_33), .out_12(out_34), .out_13(out_35), .out_14(out_36));  // open: out_10
  _4_bit_sum u_4_bit_sum_2 (
    .in_1(in_9), .in_2(in_10), .in_3(in_11), .in_4(in_12), .in_5(in_13), .in_6(in_15), .in_7(in_16),
    .in_8(in_18), .out_10(n4_bit_sum_2_out_10), .rin(n4_bit_sum_3_out_10), .out_11(out_37), .out_12(out_38),
    .out_13(out_39), .out_14(out_40));
  _4_bit_sum u_4_bit_sum_3 (
    .in_1(in_14), .in_2(in_17), .in_3(in_19), .in_4(in_20), .in_5(in_21), .in_6(in_23), .in_7(in_24),
    .in_8(in_26), .out_10(n4_bit_sum_3_out_10), .rin(n4_bit_sum_4_out_10), .out_11(out_41), .out_12(out_42),
    .out_13(out_43), .out_14(out_44));
  _4_bit_sum u_4_bit_sum_4 (
    .in_1(in_22), .in_2(in_25), .in_3(in_27), .in_4(in_28), .in_5(in_29), .in_6(in_30), .in_7(in_31),
    .in_8(in_32), .out_10(n4_bit_sum_4_out_10), .rin(1'b0), .out_11(out_45), .out_12(out_46),
    .out_13(out_47), .out_14(out_48));
endmodule

module _4_bit_to_base10 (
  input  [3:0] in_1,
  output [9:0] out_2
);

  wire not_1_out, not_2_out, not_3_out, not_4_out, not_5_out, not_6_out, not_7_out, not_8_out, not_9_out,
       not_10_out, not_11_out, not_12_out, not_13_out, not_14_out, not_15_out, not_16_out, not_17_out,
       not_18_out, not_19_out, not_20_out, not_21_out, not_22_out, not_23_out, not_24_out, not_25_out;

  not not_1 (not_1_out, in_1[0]);
  not not_2 (not_2_out, in_1[1]);
  not not_3 (not_3_out, in_1[2]);
  not not_4 (not_4_out, in_1[3]);
  not not_5 (not_5_out, in_1[1]);
  not not_6 (not_6_out, in_1[2]);
  not not_7 (not_7_out, in_1[3]);
  not not_8 (not_8_out, in_1[0]);
  not not_9 (not_9_out, in_1[2]);
  not not_10 (not_10_out, in_1[3]);
  not not_11 (not_11_out, in_1[2]);
  not not_12 (not_12_out, in_1[3]);
  not not_13 (not_13_out, in_1[0]);
  not not_14 (not_14_out, in_1[1]);
  not not_15 (not_15_out, in_1[3]);
  not not_16 (not_16_out, in_1[1]);
  not not_17 (not_17_out, in_1[3]);
  not not_18 (not_18_out, in_1[0]);
  not not_19 (not_19_out, in_1[3]);
  not not_20 (not_20_out, in_1[3]);
  not not_21 (not_21_out, in_1[0]);
  not not_22 (not_22_out, in_1[1]);
  not not_23 (not_23_out, in_1[2]);
  not not_24 (not_24_out, in_1[1]);
  not not_25 (not_25_out, in_1[2]);
  and and_1 (out_2[0], not_1_out, not_2_out, not_3_out, not_4_out);
  and and_2 (out_2[1], in_1[0], not_5_out, not_6_out, not_7_out);
  and and_3 (out_2[2], not_8_out, in_1[1], not_9_out, not_10_out);
  and and_4 (out_2[3], in_1[0], in_1[1], not_11_out, not_12_out);
  and and_5 (out_2[4], not_13_out, not_14_out, in_1[2], not_15_out);
  and and_6 (out_2[5], in_1[0], not_16_out, in_1[2], not_17_out);
  and and_7 (out_2[6], not_18_out, in_1[1], in_1[2], not_19_out);
  and and_8 (out_2[7], in_1[0], in_1[1], in_1[2], not_20_out);
  and and_9 (out_2[8], not_21_out, not_22_out, not_23_out, in_1[3]);
  and and_10 (out_2[9], in_1[0], not_24_out, not_25_out, in_1[3]);
endmodule

module base10_to_display (
  input  [9:0] in_1,
  output [6:0] out_2
);

  or or_1 (out_2[0], in_1[0], in_1[1], in_1[2], in_1[3], in_1[4], in_1[7], in_1[8], in_1[9]);
  or or_2 (out_2[2], in_1[0], in_1[4], in_1[5], in_1[6], in_1[8], in_1[9]);
  or or_3 (out_2[1], in_1[0], in_1[2], in_1[3], in_1[5], in_1[6], in_1[7], in_1[8], in_1[9]);
  or or_4 (out_2[3], in_1[3], in_1[4], in_1[5], in_1[2], in_1[6], in_1[8], in_1[9]);
  or or_5 (out_2[4], in_1[0], in_1[2], in_1[6], in_1[8]);
  or or_6 (out_2[5], in_1[0], in_1[2], in_1[3], in_1[5], in_1[6], in_1[8], in_1[9]);
  or or_7 (out_2[6], in_1[0], in_1[1], in_1[3], in_1[4], in_1[5], in_1[6], in_1[7], in_1[8], in_1[9]);
  _7_Segment_Display u_7_segment_display_1 (
    .g(out_2[3]), .f(out_2[2]), .a(out_2[1]), .b(out_2[0]), .e(out_2[4]), .d(out_2[5]), .c(out_2[6]));  // open: dp
endmodule

module bit_storage (
  input  store,
  input  reset,
  output out_3
);

  wire not_1_out, not_2_out, or_2_out;

  not not_1 (not_1_out, or_2_out);
  not not_2 (not_2_out, out_3);
  or or_1 (out_3, not_1_out, store);
  or or_2 (or_2_out, not_2_out, reset);
endmodule

module base10_to_4_bit (
  input  [9:0] in_1,
  output out_2,
  output [3:0] out_3
);

  or or_1 (out_2, in_1[0], out_3[0], out_3[1], out_3[3], out_3[2]);
  or or_2 (out_3[0], in_1[1], in_1[3], in_1[5], in_1[7], in_1[9]);
  or or_3 (out_3[1], in_1[2], in_1[6], in_1[7], in_1[3]);
  or or_4 (out_3[2], in_1[4], in_1[5], in_1[6], in_1[7]);
  or or_5 (out_3[3], in_1[8], in_1[9]);
endmodule

module _4_bit_storage (
  input  [3:0] in_1,
  input  in_2,
  output [3:0] out_3
);

  bit_storage bit_storage_1 (.store(in_1[0]), .reset(in_2), .out_3(out_3[0]));
  bit_storage bit_storage_2 (.store(in_1[1]), .reset(in_2), .out_3(out_3[1]));
  bit_storage bit_storage_3 (.store(in_1[2]), .reset(in_2), .out_3(out_3[2]));
  bit_storage bit_storage_4 (.store(in_1[3]), .reset(in_2), .out_3(out_3[3]));
endmodule

module counter (
  input  store,
  input  reset,
  output out_3,
  output out_4
);

  wire and_1_out, and_2_out, and_3_out, and_4_out, and_5_out, bit_storage_2_out_3, bit_storage_4_out_3,
       not_1_out, not_2_out, not_3_out, or_1_out, or_2_out, or_3_out;

  or or_1 (or_1_out, and_5_out, reset);
  not not_1 (not_1_out, out_3);
  and and_1 (and_1_out, not_1_out, store);
  or or_2 (or_2_out, or_1_out, out_3);
  bit_storage bit_storage_1 (.store(and_1_out), .reset(or_2_out), .out_3(out_4));
  not not_2 (not_2_out, store);
  or or_3 (or_3_out, out_4, or_1_out);
  bit_storage bit_storage_2 (.store(and_3_out), .reset(or_1_out), .out_3(bit_storage_2_out_3));
  and and_2 (and_2_out, store, bit_storage_2_out_3);
  and and_3 (and_3_out, not_2_out, out_4);
  bit_storage bit_storage_3 (.store(and_2_out), .reset(or_3_out), .out_3(out_3));
  and and_4 (and_4_out, not_3_out, out_3);
  not not_3 (not_3_out, store);
  bit_storage bit_storage_4 (.store(and_4_out), .reset(or_1_out), .out_3(bit_storage_4_out_3));
  and and_5 (and_5_out, store, bit_storage_4_out_3);
endmodule

module _8_counter (
  input  in,
  input  r,
  output _0,
  output out_4,
  output out_5,
  output out_6,
  output out_7,
  output out_8,
  output out_9,
  output _8
);

  wire counter_1_out_4, counter_2_out_4;
  wire [2:0] counter_1_out_3;
  wire [9:8] n4_bit_to_base10_1_out_2;

  counter counter_1 (.store(in), .reset(r), .out_3(counter_1_out_3[0]), .out_4(counter_1_out_4));
  counter counter_2 (.store(counter_1_out_4), .reset(r), .out_3(counter_1_out_3[1]), .out_4(counter_2_out_4));
  counter counter_3 (.store(counter_2_out_4), .reset(r), .out_3(counter_1_out_3[2]));  // open: out_4
  _4_bit_to_base10 u_4_bit_to_base10_1 (
    .in_1({1'b0, counter_1_out_3}),
    .out_2({n4_bit_to_base10_1_out_2, _8, out_9, out_8, out_7, out_6, out_5, out_4, _0}));
endmodule

module _4_bit_to_bool (
  input  [3:0] in_1,
  output out_2
);

  or or_1 (out_2, in_1[0], in_1[1], in_1[2], in_1[3]);
endmodule

module _4_bit_gateway (
  input  [3:0] in_1,
  input  in_2,
  output [3:0] out_3
);

  and and_1 (out_3[0], in_1[0], in_2);
  and and_2 (out_3[1], in_1[1], in_2);
  and and_3 (out_3[2], in_1[2], in_2);
  and and_4 (out_3[3], in_1[3], in_2);
endmodule

module input_number (
  input  counter,
  input  [3:0] in,
  input  r,
  output [3:0] out_4,
  output [3:0] out_5,
  output [3:0] out_6,
  output [3:0] out_7,
  output [3:0] out_8
);

  wire and_1_out, and_2_out, and_3_out, and_4_out, n4_bit_to_bool_1_out_2, n4_bit_to_bool_2_out_2,
       n4_bit_to_bool_3_out_2, n4_bit_to_bool_4_out_2, n4_bit_to_bool_5_out_2, n4_bit_to_bool_6_out_2,
       n4_bit_to_bool_7_out_2, n4_bit_to_bool_8_out_2, n4_bit_to_bool_9_out_2, n4_bit_to_bool_10_out_2,
       n4_bit_to_bool_11_out_2, n8_counter_1__0, n8_counter_1_out_4, n8_counter_1_out_5, n8_counter_1_out_6,
       n8_counter_1_out_7, not_1_out, not_2_out, not_3_out, not_4_out, not_5_out, not_6_out, not_7_out,
       not_8_out, not_9_out, not_10_out, not_11_out, or_1_out;
  wire [3:0] _11, _21, _22, _31, _32, _33, _41, _42, _43, _44, _52, _53, _54, _55, n4_bit_gateway_1_out_3,
       n4_bit_gateway_2_out_3, n4_bit_gateway_3_out_3, n4_bit_gateway_4_out_3, n4_bit_gateway_5_out_3,
       n4_bit_gateway_6_out_3, n4_bit_gateway_7_out_3, n4_bit_gateway_8_out_3, n4_bit_gateway_9_out_3,
       n4_bit_gateway_10_out_3, n4_bit_gateway_11_out_3, n4_bit_gateway_12_out_3, n4_bit_gateway_13_out_3,
       n4_bit_gateway_14_out_3, n4_bit_gateway_15_out_3, n4_bit_gateway_16_out_3, n4_bit_gateway_17_out_3,
       n4_bit_gateway_18_out_3, n4_bit_gateway_19_out_3, n4_bit_gateway_20_out_3, n4_bit_gateway_21_out_3,
       n4_bit_gateway_22_out_3, n4_bit_gateway_23_out_3, n4_bit_gateway_24_out_3, n4_bit_gateway_25_out_3,
       n4_bit_gateway_26_out_3, n4_bit_gateway_27_out_3, n4_bit_gateway_28_out_3, n4_bit_gateway_29_out_3,
       n4_bit_storage_1_out_3, new_4_bit_sum_3_out_3, new_4_bit_sum_4_out_3, new_4_bit_sum_6_out_3,
       new_4_bit_sum_7_out_3, new_4_bit_sum_8_out_3, new_4_bit_sum_9_out_3, new_4_bit_sum_11_out_3,
       new_4_bit_sum_12_out_3, new_4_bit_sum_13_out_3, new_4_bit_sum_14_out_3;

  _4_bit_to_bool u_4_bit_to_bool_1 (.in_1(in), .out_2(n4_bit_to_bool_1_out_2));
  or or_1 (or_1_out, r, n4_bit_to_bool_1_out_2);
  _4_bit_storage u_4_bit_storage_1 (.in_1(in), .in_2(or_1_out), .out_3(n4_bit_storage_1_out_3));
  _4_bit_gateway u_4_bit_gateway_1 (
    .in_1(n4_bit_storage_1_out_3), .in_2(n8_counter_1__0), .out_3(n4_bit_gateway_1_out_3));
  _4_bit_gateway u_4_bit_gateway_2 (.in_1(_21), .in_2(not_2_out), .out_3(n4_bit_gateway_2_out_3));
  new_4_bit_sum new_4_bit_sum_1 (.out_3(out_7), .in_1(n4_bit_gateway_2_out_3), .in_2(new_4_bit_sum_4_out_3));
  and and_1 (and_1_out, n4_bit_to_bool_1_out_2, n8_counter_1_out_4);
  _4_bit_storage u_4_bit_storage_2 (.in_1(n4_bit_gateway_1_out_3), .in_2(r), .out_3(_11));
  not not_1 (not_1_out, n4_bit_to_bool_2_out_2);
  _4_bit_to_bool u_4_bit_to_bool_2 (.in_1(new_4_bit_sum_3_out_3), .out_2(n4_bit_to_bool_2_out_2));
  _4_bit_gateway u_4_bit_gateway_3 (.in_1(_41), .in_2(not_1_out), .out_3(n4_bit_gateway_3_out_3));
  new_4_bit_sum new_4_bit_sum_2 (.out_3(out_5), .in_1(n4_bit_gateway_3_out_3), .in_2(new_4_bit_sum_3_out_3));
  not not_2 (not_2_out, n4_bit_to_bool_3_out_2);
  _4_bit_to_bool u_4_bit_to_bool_3 (.in_1(new_4_bit_sum_4_out_3), .out_2(n4_bit_to_bool_3_out_2));
  _4_bit_storage u_4_bit_storage_3 (.in_1(n4_bit_gateway_4_out_3), .in_2(r), .out_3(_21));
  _4_bit_gateway u_4_bit_gateway_4 (.in_1(_11), .in_2(and_1_out), .out_3(n4_bit_gateway_4_out_3));
  _4_bit_storage u_4_bit_storage_4 (.in_1(n4_bit_gateway_5_out_3), .in_2(r), .out_3(_22));
  _4_bit_gateway u_4_bit_gateway_5 (.in_1(n4_bit_storage_1_out_3), .in_2(and_1_out), .out_3(n4_bit_gateway_5_out_3));
  _4_bit_gateway u_4_bit_gateway_6 (.in_1(_52), .in_2(1'b1), .out_3(n4_bit_gateway_6_out_3));
  new_4_bit_sum new_4_bit_sum_3 (.out_3(new_4_bit_sum_3_out_3), .in_1(n4_bit_gateway_6_out_3), .in_2(4'b0000));
  not not_3 (not_3_out, n4_bit_to_bool_4_out_2);
  _4_bit_gateway u_4_bit_gateway_7 (.in_1(_32), .in_2(not_3_out), .out_3(n4_bit_gateway_7_out_3));
  new_4_bit_sum new_4_bit_sum_4 (
    .out_3(new_4_bit_sum_4_out_3), .in_1(n4_bit_gateway_7_out_3), .in_2(new_4_bit_sum_6_out_3));
  and and_2 (and_2_out, n4_bit_to_bool_1_out_2, n8_counter_1_out_5);
  _4_bit_gateway u_4_bit_gateway_8 (.in_1(_31), .in_2(not_5_out), .out_3(n4_bit_gateway_8_out_3));
  new_4_bit_sum new_4_bit_sum_5 (.out_3(out_6), .in_1(n4_bit_gateway_8_out_3), .in_2(new_4_bit_sum_7_out_3));
  _4_bit_to_bool u_4_bit_to_bool_4 (.in_1(new_4_bit_sum_6_out_3), .out_2(n4_bit_to_bool_4_out_2));
  not not_4 (not_4_out, counter);
  _8_counter u_8_counter_1 (
    .in(not_4_out), .r(r), ._0(n8_counter_1__0), .out_4(n8_counter_1_out_4), .out_5(n8_counter_1_out_5),
    .out_6(n8_counter_1_out_6), .out_7(n8_counter_1_out_7));  // open: out_8, out_9, _8
  _4_bit_gateway u_4_bit_gateway_9 (.in_1(_21), .in_2(and_2_out), .out_3(n4_bit_gateway_9_out_3));
  _4_bit_storage u_4_bit_storage_5 (.in_1(n4_bit_gateway_9_out_3), .in_2(r), .out_3(_31));
  _4_bit_gateway u_4_bit_gateway_10 (.in_1(_22), .in_2(and_2_out), .out_3(n4_bit_gateway_10_out_3));
  _4_bit_storage u_4_bit_storage_6 (.in_1(n4_bit_gateway_10_out_3), .in_2(r), .out_3(_32));
  _4_bit_storage u_4_bit_storage_7 (.in_1(n4_bit_gateway_11_out_3), .in_2(r), .out_3(_33));
  _4_bit_gateway u_4_bit_gateway_11 (.in_1(n4_bit_storage_1_out_3), .in_2(and_2_out), .out_3(n4_bit_gateway_11_out_3));
  not not_5 (not_5_out, n4_bit_to_bool_5_out_2);
  _4_bit_to_bool u_4_bit_to_bool_5 (.in_1(new_4_bit_sum_7_out_3), .out_2(n4_bit_to_bool_5_out_2));
  not not_6 (not_6_out, n4_bit_to_bool_6_out_2);
  _4_bit_gateway u_4_bit_gateway_12 (.in_1(_43), .in_2(not_6_out), .out_3(n4_bit_gateway_12_out_3));
  new_4_bit_sum new_4_bit_sum_6 (
    .out_3(new_4_bit_sum_6_out_3), .in_1(n4_bit_gateway_12_out_3), .in_2(new_4_bit_sum_8_out_3));
  and and_3 (and_3_out, n4_bit_to_bool_1_out_2, n8_counter_1_out_6);
  not not_7 (not_7_out, n4_bit_to_bool_7_out_2);
  _4_bit_gateway u_4_bit_gateway_13 (.in_1(_42), .in_2(not_7_out), .out_3(n4_bit_gateway_13_out_3));
  new_4_bit_sum new_4_bit_sum_7 (
    .out_3(new_4_bit_sum_7_out_3), .in_1(n4_bit_gateway_13_out_3), .in_2(new_4_bit_sum_9_out_3));
  _4_bit_to_bool u_4_bit_to_bool_6 (.in_1(new_4_bit_sum_8_out_3), .out_2(n4_bit_to_bool_6_out_2));
  _4_bit_storage u_4_bit_storage_8 (.in_1(n4_bit_gateway_14_out_3), .in_2(r), .out_3(_41));
  _4_bit_gateway u_4_bit_gateway_14 (.in_1(_31), .in_2(and_3_out), .out_3(n4_bit_gateway_14_out_3));
  _4_bit_storage u_4_bit_storage_9 (.in_1(n4_bit_gateway_15_out_3), .in_2(r), .out_3(_42));
  _4_bit_gateway u_4_bit_gateway_15 (.in_1(_32), .in_2(and_3_out), .out_3(n4_bit_gateway_15_out_3));
  _4_bit_storage u_4_bit_storage_10 (.in_1(n4_bit_gateway_16_out_3), .in_2(r), .out_3(_43));
  _4_bit_gateway u_4_bit_gateway_16 (.in_1(_33), .in_2(and_3_out), .out_3(n4_bit_gateway_16_out_3));
  _4_bit_gateway u_4_bit_gateway_17 (.in_1(n4_bit_storage_1_out_3), .in_2(and_3_out), .out_3(n4_bit_gateway_17_out_3));
  _4_bit_storage u_4_bit_storage_11 (.in_1(n4_bit_gateway_17_out_3), .in_2(r), .out_3(_44));
  _4_bit_to_bool u_4_bit_to_bool_7 (.in_1(new_4_bit_sum_9_out_3), .out_2(n4_bit_to_bool_7_out_2));
  _4_bit_gateway u_4_bit_gateway_18 (.in_1(_54), .in_2(1'b1), .out_3(n4_bit_gateway_18_out_3));
  new_4_bit_sum new_4_bit_sum_8 (.out_3(new_4_bit_sum_8_out_3), .in_1(n4_bit_gateway_18_out_3), .in_2(4'b0000));
  _4_bit_gateway u_4_bit_gateway_19 (.in_1(_53), .in_2(1'b1), .out_3(n4_bit_gateway_19_out_3));
  new_4_bit_sum new_4_bit_sum_9 (.out_3(new_4_bit_sum_9_out_3), .in_1(n4_bit_gateway_19_out_3), .in_2(4'b0000));
  not not_8 (not_8_out, n4_bit_to_bool_8_out_2);
  _4_bit_gateway u_4_bit_gateway_20 (.in_1(_11), .in_2(not_8_out), .out_3(n4_bit_gateway_20_out_3));
  new_4_bit_sum new_4_bit_sum_10 (.out_3(out_8), .in_1(n4_bit_gateway_20_out_3), .in_2(new_4_bit_sum_11_out_3));
  and and_4 (and_4_out, n4_bit_to_bool_1_out_2, n8_counter_1_out_7);
  _4_bit_gateway u_4_bit_gateway_21 (.in_1(_41), .in_2(and_4_out), .out_3(n4_bit_gateway_21_out_3));
  _4_bit_gateway u_4_bit_gateway_22 (.in_1(_42), .in_2(and_4_out), .out_3(n4_bit_gateway_22_out_3));
  _4_bit_gateway u_4_bit_gateway_23 (.in_1(_43), .in_2(and_4_out), .out_3(n4_bit_gateway_23_out_3));
  _4_bit_gateway u_4_bit_gateway_24 (.in_1(_44), .in_2(and_4_out), .out_3(n4_bit_gateway_24_out_3));
  _4_bit_gateway u_4_bit_gateway_25 (.in_1(n4_bit_storage_1_out_3), .in_2(and_4_out), .out_3(n4_bit_gateway_25_out_3));
  _4_bit_to_bool u_4_bit_to_bool_8 (.in_1(new_4_bit_sum_11_out_3), .out_2(n4_bit_to_bool_8_out_2));
  _4_bit_storage u_4_bit_storage_12 (.in_1(n4_bit_gateway_21_out_3), .in_2(r), .out_3(out_4));
  _4_bit_storage u_4_bit_storage_13 (.in_1(n4_bit_gateway_22_out_3), .in_2(r), .out_3(_52));
  _4_bit_storage u_4_bit_storage_14 (.in_1(n4_bit_gateway_23_out_3), .in_2(r), .out_3(_53));
  _4_bit_storage u_4_bit_storage_15 (.in_1(n4_bit_gateway_24_out_3), .in_2(r), .out_3(_54));
  _4_bit_storage u_4_bit_storage_16 (.in_1(n4_bit_gateway_25_out_3), .in_2(r), .out_3(_55));
  not not_9 (not_9_out, n4_bit_to_bool_9_out_2);
  _4_bit_gateway u_4_bit_gateway_26 (.in_1(_22), .in_2(not_9_out), .out_3(n4_bit_gateway_26_out_3));
  new_4_bit_sum new_4_bit_sum_11 (
    .out_3(new_4_bit_sum_11_out_3), .in_1(n4_bit_gateway_26_out_3), .in_2(new_4_bit_sum_12_out_3));
  _4_bit_to_bool u_4_bit_to_bool_9 (.in_1(new_4_bit_sum_12_out_3), .out_2(n4_bit_to_bool_9_out_2));
  not not_10 (not_10_out, n4_bit_to_bool_10_out_2);
  _4_bit_to_bool u_4_bit_to_bool_10 (.in_1(new_4_bit_sum_13_out_3), .out_2(n4_bit_to_bool_10_out_2));
  _4_bit_gateway u_4_bit_gateway_27 (.in_1(_33), .in_2(not_10_out), .out_3(n4_bit_gateway_27_out_3));
  new_4_bit_sum new_4_bit_sum_12 (
    .out_3(new_4_bit_sum_12_out_3), .in_1(n4_bit_gateway_27_out_3), .in_2(new_4_bit_sum_13_out_3));
  not not_11 (not_11_out, n4_bit_to_bool_11_out_2);
  _4_bit_to_bool u_4_bit_to_bool_11 (.in_1(new_4_bit_sum_14_out_3), .out_2(n4_bit_to_bool_11_out_2));
  _4_bit_gateway u_4_bit_gateway_28 (.in_1(_44), .in_2(not_11_out), .out_3(n4_bit_gateway_28_out_3));
  new_4_bit_sum new_4_bit_sum_13 (
    .out_3(new_4_bit_sum_13_out_3), .in_1(n4_bit_gateway_28_out_3), .in_2(new_4_bit_sum_14_out_3));
  new_4_bit_sum new_4_bit_sum_14 (.out_3(new_4_bit_sum_14_out_3), .in_1(n4_bit_gateway_29_out_3), .in_2(4'b0000));
  _4_bit_gateway u_4_bit_gateway_29 (.in_1(_55), .in_2(1'b1), .out_3(n4_bit_gateway_29_out_3));

  // Other names for the same wires on the sheet: _51[3:0] = out_4
endmodule

module new_4_bit_sum (
  input  [3:0] in_1,
  input  [3:0] in_2,
  output [3:0] out_3
);

  _4_bit_sum u_4_bit_sum_1 (
    .in_1(in_1[0]), .in_2(in_1[1]), .in_3(in_1[2]), .in_4(in_1[3]), .in_5(in_2[0]), .in_6(in_2[1]),
    .in_7(in_2[2]), .in_8(in_2[3]), .rin(1'b0), .out_11(out_3[0]), .out_12(out_3[1]), .out_13(out_3[2]),
    .out_14(out_3[3]));  // open: out_10
endmodule

module addition (
  input  [15:0] in_1,
  input  [15:0] in_2,
  output [15:0] out_3
);

  _16_bit_addition u_16_bit_addition_1 (
    .in_2(in_1[15]), .in_3(in_1[14]), .in_5(in_1[13]), .in_6(in_1[12]), .in_13(in_1[11]), .in_15(in_1[10]),
    .in_16(in_1[9]), .in_18(in_1[8]), .in_21(in_1[7]), .in_23(in_1[6]), .in_24(in_1[5]), .in_26(in_1[4]),
    .in_29(in_1[3]), .in_30(in_1[2]), .in_31(in_1[1]), .in_32(in_1[0]), .out_34(out_3[15]),
    .out_33(out_3[14]), .out_35(out_3[13]), .out_36(out_3[12]), .out_37(out_3[11]), .out_38(out_3[10]),
    .out_39(out_3[9]), .out_40(out_3[8]), .out_41(out_3[7]), .out_42(out_3[6]), .out_43(out_3[5]),
    .out_44(out_3[4]), .out_45(out_3[3]), .out_46(out_3[2]), .out_47(out_3[1]), .out_48(out_3[0]),
    .in_1(in_2[15]), .in_4(in_2[14]), .in_7(in_2[13]), .in_8(in_2[12]), .in_9(in_2[11]), .in_10(in_2[10]),
    .in_11(in_2[9]), .in_12(in_2[8]), .in_14(in_2[7]), .in_17(in_2[6]), .in_19(in_2[5]), .in_20(in_2[4]),
    .in_22(in_2[3]), .in_25(in_2[2]), .in_27(in_2[1]), .in_28(in_2[0]));
endmodule

module _16_bit_x10 (
  input  [15:0] in_1,
  output [15:0] out_2
);

  addition addition_1 (.in_1({in_1[12:0], 3'b000}), .in_2({in_1[14:0], 1'b0}), .out_3(out_2));
endmodule

module input_to_binary (
  input  [19:0] in_1,
  output [15:0] out_2
);

  wire [15:0] addition_1_out_3, addition_2_out_3, addition_4_out_3, n16_bit_x10_1_out_2, n16_bit_x10_2_out_2,
       n16_bit_x10_3_out_2, n16_bit_x10_4_out_2, n16_bit_x10_5_out_2, n16_bit_x10_6_out_2,
       n16_bit_x10_7_out_2, n16_bit_x10_8_out_2, n16_bit_x10_9_out_2, n16_bit_x10_10_out_2;

  _16_bit_x10 u_16_bit_x10_1 (.in_1(n16_bit_x10_2_out_2), .out_2(n16_bit_x10_1_out_2));
  _16_bit_x10 u_16_bit_x10_2 (.in_1({{12{1'b0}}, in_1[3:0]}), .out_2(n16_bit_x10_2_out_2));
  _16_bit_x10 u_16_bit_x10_3 (.in_1(n16_bit_x10_1_out_2), .out_2(n16_bit_x10_3_out_2));
  _16_bit_x10 u_16_bit_x10_4 (.in_1({{12{1'b0}}, in_1[7:4]}), .out_2(n16_bit_x10_4_out_2));
  _16_bit_x10 u_16_bit_x10_5 (.in_1(n16_bit_x10_6_out_2), .out_2(n16_bit_x10_5_out_2));
  _16_bit_x10 u_16_bit_x10_6 (.in_1(n16_bit_x10_4_out_2), .out_2(n16_bit_x10_6_out_2));
  _16_bit_x10 u_16_bit_x10_7 (.in_1({{12{1'b0}}, in_1[11:8]}), .out_2(n16_bit_x10_7_out_2));
  _16_bit_x10 u_16_bit_x10_8 (.in_1(n16_bit_x10_7_out_2), .out_2(n16_bit_x10_8_out_2));
  _16_bit_x10 u_16_bit_x10_9 (.in_1({{12{1'b0}}, in_1[15:12]}), .out_2(n16_bit_x10_9_out_2));
  addition addition_1 (.in_1(n16_bit_x10_9_out_2), .in_2({{12{1'b0}}, in_1[19:16]}), .out_3(addition_1_out_3));
  _16_bit_x10 u_16_bit_x10_10 (.in_1(n16_bit_x10_3_out_2), .out_2(n16_bit_x10_10_out_2));
  addition addition_2 (.in_1(n16_bit_x10_8_out_2), .in_2(addition_1_out_3), .out_3(addition_2_out_3));
  addition addition_3 (.in_1(n16_bit_x10_10_out_2), .in_2(addition_4_out_3), .out_3(out_2));
  addition addition_4 (.in_1(n16_bit_x10_5_out_2), .in_2(addition_2_out_3), .out_3(addition_4_out_3));
endmodule

module _1_bit_sub (
  input  in_1,
  input  in_2,
  input  in_3,
  output out_4,
  output out_5
);

  wire and_1_out, and_2_out, and_3_out, and_4_out, and_5_out, not_1_out, not_2_out, not_3_out, or_1_out;

  and and_1 (and_1_out, not_1_out, and_2_out);
  not not_1 (not_1_out, in_1);
  and and_2 (and_2_out, or_1_out, not_2_out);
  not not_2 (not_2_out, and_3_out);
  or or_1 (or_1_out, in_2, in_3);
  or or_2 (out_4, and_1_out, and_3_out);
  and and_3 (and_3_out, in_2, in_3);
  and and_4 (and_4_out, in_1, and_3_out);
  and and_5 (and_5_out, in_1, not_3_out);
  not not_3 (not_3_out, or_1_out);
  or or_3 (out_5, and_4_out, and_5_out, and_1_out);
endmodule

module subtraction (
  input  [15:0] in_1,
  input  [15:0] in_2,
  output [15:0] out_3
);

  wire n1_bit_sub_2_out_4, n1_bit_sub_3_out_4, n1_bit_sub_4_out_4, n1_bit_sub_5_out_4, n1_bit_sub_6_out_4,
       n1_bit_sub_7_out_4, n1_bit_sub_8_out_4, n1_bit_sub_9_out_4, n1_bit_sub_10_out_4, n1_bit_sub_11_out_4,
       n1_bit_sub_12_out_4, n1_bit_sub_13_out_4, n1_bit_sub_14_out_4, n1_bit_sub_15_out_4,
       n1_bit_sub_16_out_4;

  _1_bit_sub u_1_bit_sub_1 (
    .in_1(in_1[15]), .in_2(in_2[15]), .in_3(n1_bit_sub_2_out_4), .out_5(out_3[15]));  // open: out_4
  _1_bit_sub u_1_bit_sub_2 (
    .in_1(in_1[14]), .in_2(in_2[14]), .out_4(n1_bit_sub_2_out_4), .in_3(n1_bit_sub_3_out_4), .out_5(out_3[14]));
  _1_bit_sub u_1_bit_sub_3 (
    .in_1(in_1[13]), .in_2(in_2[13]), .out_4(n1_bit_sub_3_out_4), .in_3(n1_bit_sub_4_out_4), .out_5(out_3[13]));
  _1_bit_sub u_1_bit_sub_4 (
    .in_1(in_1[12]), .in_2(in_2[12]), .out_4(n1_bit_sub_4_out_4), .in_3(n1_bit_sub_5_out_4), .out_5(out_3[12]));
  _1_bit_sub u_1_bit_sub_5 (
    .in_1(in_1[11]), .in_2(in_2[11]), .out_4(n1_bit_sub_5_out_4), .in_3(n1_bit_sub_6_out_4), .out_5(out_3[11]));
  _1_bit_sub u_1_bit_sub_6 (
    .in_1(in_1[10]), .in_2(in_2[10]), .out_4(n1_bit_sub_6_out_4), .in_3(n1_bit_sub_7_out_4), .out_5(out_3[10]));
  _1_bit_sub u_1_bit_sub_7 (
    .in_1(in_1[9]), .in_2(in_2[9]), .out_4(n1_bit_sub_7_out_4), .in_3(n1_bit_sub_8_out_4), .out_5(out_3[9]));
  _1_bit_sub u_1_bit_sub_8 (
    .in_1(in_1[8]), .in_2(in_2[8]), .out_4(n1_bit_sub_8_out_4), .in_3(n1_bit_sub_9_out_4), .out_5(out_3[8]));
  _1_bit_sub u_1_bit_sub_9 (
    .in_1(in_1[7]), .in_2(in_2[7]), .out_4(n1_bit_sub_9_out_4), .in_3(n1_bit_sub_10_out_4), .out_5(out_3[7]));
  _1_bit_sub u_1_bit_sub_10 (
    .in_1(in_1[6]), .in_2(in_2[6]), .out_4(n1_bit_sub_10_out_4), .in_3(n1_bit_sub_11_out_4), .out_5(out_3[6]));
  _1_bit_sub u_1_bit_sub_11 (
    .in_1(in_1[5]), .in_2(in_2[5]), .out_4(n1_bit_sub_11_out_4), .in_3(n1_bit_sub_12_out_4), .out_5(out_3[5]));
  _1_bit_sub u_1_bit_sub_12 (
    .in_1(in_1[4]), .in_2(in_2[4]), .out_4(n1_bit_sub_12_out_4), .in_3(n1_bit_sub_13_out_4), .out_5(out_3[4]));
  _1_bit_sub u_1_bit_sub_13 (
    .in_1(in_1[3]), .in_2(in_2[3]), .out_4(n1_bit_sub_13_out_4), .in_3(n1_bit_sub_14_out_4), .out_5(out_3[3]));
  _1_bit_sub u_1_bit_sub_14 (
    .in_1(in_1[2]), .in_2(in_2[2]), .out_4(n1_bit_sub_14_out_4), .in_3(n1_bit_sub_15_out_4), .out_5(out_3[2]));
  _1_bit_sub u_1_bit_sub_15 (
    .in_1(in_1[1]), .in_2(in_2[1]), .out_4(n1_bit_sub_15_out_4), .in_3(n1_bit_sub_16_out_4), .out_5(out_3[1]));
  _1_bit_sub u_1_bit_sub_16 (
    .in_1(in_1[0]), .in_2(in_2[0]), .out_4(n1_bit_sub_16_out_4), .in_3(1'b0), .out_5(out_3[0]));
endmodule

module _16_bit_gateway (
  input  [15:0] in_1,
  input  in_2,
  output [15:0] out_3
);

  _4_bit_gateway u_4_bit_gateway_1 (.in_1(in_1[3:0]), .in_2(in_2), .out_3(out_3[3:0]));
  _4_bit_gateway u_4_bit_gateway_2 (.in_1(in_1[7:4]), .in_2(in_2), .out_3(out_3[7:4]));
  _4_bit_gateway u_4_bit_gateway_3 (.in_1(in_1[11:8]), .in_2(in_2), .out_3(out_3[11:8]));
  _4_bit_gateway u_4_bit_gateway_4 (.in_1(in_1[15:12]), .in_2(in_2), .out_3(out_3[15:12]));
endmodule

module multiplication (
  input  [15:0] in_1,
  input  [15:0] in_2,
  output [15:0] out_3
);

  wire [15:0] addition_1_out_3, addition_2_out_3, addition_3_out_3, addition_4_out_3, addition_5_out_3,
       addition_6_out_3, addition_7_out_3, addition_8_out_3, addition_9_out_3, addition_10_out_3,
       addition_11_out_3, addition_12_out_3, addition_13_out_3, addition_14_out_3, addition_16_out_3,
       n16_bit_gateway_1_out_3, n16_bit_gateway_2_out_3, n16_bit_gateway_3_out_3, n16_bit_gateway_4_out_3,
       n16_bit_gateway_5_out_3, n16_bit_gateway_6_out_3, n16_bit_gateway_7_out_3, n16_bit_gateway_8_out_3,
       n16_bit_gateway_9_out_3, n16_bit_gateway_10_out_3, n16_bit_gateway_11_out_3, n16_bit_gateway_12_out_3,
       n16_bit_gateway_13_out_3, n16_bit_gateway_14_out_3, n16_bit_gateway_15_out_3,
       n16_bit_gateway_16_out_3, n16_bit_shift_up_1_out_2, n16_bit_shift_up_2_out_2,
       n16_bit_shift_up_3_out_2, n16_bit_shift_up_4_out_2, n16_bit_shift_up_5_out_2,
       n16_bit_shift_up_6_out_2, n16_bit_shift_up_7_out_2, n16_bit_shift_up_8_out_2,
       n16_bit_shift_up_9_out_2, n16_bit_shift_up_10_out_2, n16_bit_shift_up_11_out_2,
       n16_bit_shift_up_12_out_2, n16_bit_shift_up_13_out_2, n16_bit_shift_up_14_out_2,
       n16_bit_shift_up_15_out_2, n16_bit_shift_up_16_out_2, n16_bit_shift_up_17_out_2,
       n16_bit_shift_up_18_out_2, n16_bit_shift_up_19_out_2, n16_bit_shift_up_20_out_2,
       n16_bit_shift_up_21_out_2, n16_bit_shift_up_22_out_2, n16_bit_shift_up_23_out_2,
       n16_bit_shift_up_24_out_2, n16_bit_shift_up_25_out_2, n16_bit_shift_up_26_out_2,
       n16_bit_shift_up_27_out_2, n16_bit_shift_up_28_out_2, n16_bit_shift_up_29_out_2,
       n16_bit_shift_up_30_out_2, n16_bit_shift_up_31_out_2, n16_bit_shift_up_32_out_2,
       n16_bit_shift_up_33_out_2, n16_bit_shift_up_34_out_2, n16_bit_shift_up_35_out_2,
       n16_bit_shift_up_36_out_2, n16_bit_shift_up_37_out_2, n16_bit_shift_up_38_out_2,
       n16_bit_shift_up_39_out_2, n16_bit_shift_up_40_out_2, n16_bit_shift_up_41_out_2,
       n16_bit_shift_up_42_out_2, n16_bit_shift_up_43_out_2, n16_bit_shift_up_44_out_2,
       n16_bit_shift_up_45_out_2, n16_bit_shift_up_46_out_2, n16_bit_shift_up_47_out_2,
       n16_bit_shift_up_48_out_2, n16_bit_shift_up_49_out_2, n16_bit_shift_up_50_out_2,
       n16_bit_shift_up_51_out_2, n16_bit_shift_up_52_out_2, n16_bit_shift_up_53_out_2,
       n16_bit_shift_up_54_out_2, n16_bit_shift_up_55_out_2, n16_bit_shift_up_56_out_2,
       n16_bit_shift_up_57_out_2, n16_bit_shift_up_58_out_2, n16_bit_shift_up_59_out_2,
       n16_bit_shift_up_60_out_2, n16_bit_shift_up_61_out_2, n16_bit_shift_up_62_out_2,
       n16_bit_shift_up_63_out_2, n16_bit_shift_up_64_out_2, n16_bit_shift_up_65_out_2,
       n16_bit_shift_up_66_out_2, n16_bit_shift_up_67_out_2, n16_bit_shift_up_68_out_2,
       n16_bit_shift_up_69_out_2, n16_bit_shift_up_70_out_2, n16_bit_shift_up_71_out_2,
       n16_bit_shift_up_72_out_2, n16_bit_shift_up_73_out_2, n16_bit_shift_up_74_out_2,
       n16_bit_shift_up_75_out_2, n16_bit_shift_up_76_out_2, n16_bit_shift_up_77_out_2,
       n16_bit_shift_up_78_out_2, n16_bit_shift_up_79_out_2, n16_bit_shift_up_80_out_2,
       n16_bit_shift_up_81_out_2, n16_bit_shift_up_82_out_2, n16_bit_shift_up_83_out_2,
       n16_bit_shift_up_84_out_2, n16_bit_shift_up_85_out_2, n16_bit_shift_up_86_out_2,
       n16_bit_shift_up_87_out_2, n16_bit_shift_up_88_out_2, n16_bit_shift_up_89_out_2,
       n16_bit_shift_up_90_out_2, n16_bit_shift_up_91_out_2, n16_bit_shift_up_92_out_2,
       n16_bit_shift_up_93_out_2, n16_bit_shift_up_94_out_2, n16_bit_shift_up_95_out_2,
       n16_bit_shift_up_96_out_2, n16_bit_shift_up_97_out_2, n16_bit_shift_up_98_out_2,
       n16_bit_shift_up_99_out_2, n16_bit_shift_up_100_out_2, n16_bit_shift_up_101_out_2,
       n16_bit_shift_up_102_out_2, n16_bit_shift_up_103_out_2, n16_bit_shift_up_104_out_2,
       n16_bit_shift_up_105_out_2, n16_bit_shift_up_106_out_2, n16_bit_shift_up_107_out_2,
       n16_bit_shift_up_108_out_2, n16_bit_shift_up_109_out_2, n16_bit_shift_up_110_out_2,
       n16_bit_shift_up_111_out_2, n16_bit_shift_up_112_out_2, n16_bit_shift_up_113_out_2,
       n16_bit_shift_up_114_out_2, n16_bit_shift_up_115_out_2, n16_bit_shift_up_116_out_2,
       n16_bit_shift_up_117_out_2, n16_bit_shift_up_118_out_2, n16_bit_shift_up_119_out_2,
       n16_bit_shift_up_120_out_2;

  _16_bit_shift_up u_16_bit_shift_up_1 (.in_1(n16_bit_gateway_1_out_3), .out_2(n16_bit_shift_up_1_out_2));
  _16_bit_gateway u_16_bit_gateway_1 (.in_1(in_2), .in_2(in_1[15]), .out_3(n16_bit_gateway_1_out_3));
  _16_bit_shift_up u_16_bit_shift_up_2 (.in_1(n16_bit_shift_up_1_out_2), .out_2(n16_bit_shift_up_2_out_2));
  _16_bit_gateway u_16_bit_gateway_2 (.in_1(in_2), .in_2(in_1[14]), .out_3(n16_bit_gateway_2_out_3));
  _16_bit_shift_up u_16_bit_shift_up_3 (.in_1(n16_bit_shift_up_4_out_2), .out_2(n16_bit_shift_up_3_out_2));
  _16_bit_shift_up u_16_bit_shift_up_4 (.in_1(n16_bit_gateway_2_out_3), .out_2(n16_bit_shift_up_4_out_2));
  _16_bit_shift_up u_16_bit_shift_up_5 (.in_1(n16_bit_shift_up_6_out_2), .out_2(n16_bit_shift_up_5_out_2));
  _16_bit_shift_up u_16_bit_shift_up_6 (.in_1(n16_bit_gateway_3_out_3), .out_2(n16_bit_shift_up_6_out_2));
  _16_bit_gateway u_16_bit_gateway_3 (.in_1(in_2), .in_2(in_1[13]), .out_3(n16_bit_gateway_3_out_3));
  _16_bit_shift_up u_16_bit_shift_up_7 (.in_1(n16_bit_shift_up_8_out_2), .out_2(n16_bit_shift_up_7_out_2));
  _16_bit_shift_up u_16_bit_shift_up_8 (.in_1(n16_bit_gateway_4_out_3), .out_2(n16_bit_shift_up_8_out_2));
  _16_bit_gateway u_16_bit_gateway_4 (.in_1(in_2), .in_2(in_1[12]), .out_3(n16_bit_gateway_4_out_3));
  _16_bit_gateway u_16_bit_gateway_5 (.in_1(in_2), .in_2(in_1[11]), .out_3(n16_bit_gateway_5_out_3));
  _16_bit_shift_up u_16_bit_shift_up_9 (.in_1(n16_bit_shift_up_10_out_2), .out_2(n16_bit_shift_up_9_out_2));
  _16_bit_shift_up u_16_bit_shift_up_10 (.in_1(n16_bit_gateway_5_out_3), .out_2(n16_bit_shift_up_10_out_2));
  _16_bit_shift_up u_16_bit_shift_up_11 (.in_1(n16_bit_gateway_6_out_3), .out_2(n16_bit_shift_up_11_out_2));
  _16_bit_gateway u_16_bit_gateway_6 (.in_1(in_2), .in_2(in_1[10]), .out_3(n16_bit_gateway_6_out_3));
  _16_bit_shift_up u_16_bit_shift_up_12 (.in_1(n16_bit_shift_up_11_out_2), .out_2(n16_bit_shift_up_12_out_2));
  _16_bit_gateway u_16_bit_gateway_7 (.in_1(in_2), .in_2(in_1[9]), .out_3(n16_bit_gateway_7_out_3));
  _16_bit_shift_up u_16_bit_shift_up_13 (.in_1(n16_bit_shift_up_14_out_2), .out_2(n16_bit_shift_up_13_out_2));
  _16_bit_shift_up u_16_bit_shift_up_14 (.in_1(n16_bit_gateway_7_out_3), .out_2(n16_bit_shift_up_14_out_2));
  _16_bit_shift_up u_16_bit_shift_up_15 (.in_1(n16_bit_gateway_8_out_3), .out_2(n16_bit_shift_up_15_out_2));
  _16_bit_gateway u_16_bit_gateway_8 (.in_1(in_2), .in_2(in_1[8]), .out_3(n16_bit_gateway_8_out_3));
  _16_bit_shift_up u_16_bit_shift_up_16 (.in_1(n16_bit_shift_up_15_out_2), .out_2(n16_bit_shift_up_16_out_2));
  _16_bit_shift_up u_16_bit_shift_up_17 (.in_1(n16_bit_shift_up_18_out_2), .out_2(n16_bit_shift_up_17_out_2));
  _16_bit_shift_up u_16_bit_shift_up_18 (.in_1(n16_bit_gateway_9_out_3), .out_2(n16_bit_shift_up_18_out_2));
  _16_bit_gateway u_16_bit_gateway_9 (.in_1(in_2), .in_2(in_1[7]), .out_3(n16_bit_gateway_9_out_3));
  _16_bit_shift_up u_16_bit_shift_up_19 (.in_1(n16_bit_shift_up_20_out_2), .out_2(n16_bit_shift_up_19_out_2));
  _16_bit_shift_up u_16_bit_shift_up_20 (.in_1(n16_bit_gateway_10_out_3), .out_2(n16_bit_shift_up_20_out_2));
  _16_bit_gateway u_16_bit_gateway_10 (.in_1(in_2), .in_2(in_1[6]), .out_3(n16_bit_gateway_10_out_3));
  _16_bit_shift_up u_16_bit_shift_up_21 (.in_1(n16_bit_gateway_11_out_3), .out_2(n16_bit_shift_up_21_out_2));
  _16_bit_shift_up u_16_bit_shift_up_22 (.in_1(n16_bit_shift_up_21_out_2), .out_2(n16_bit_shift_up_22_out_2));
  _16_bit_gateway u_16_bit_gateway_11 (.in_1(in_2), .in_2(in_1[5]), .out_3(n16_bit_gateway_11_out_3));
  _16_bit_shift_up u_16_bit_shift_up_23 (.in_1(n16_bit_shift_up_24_out_2), .out_2(n16_bit_shift_up_23_out_2));
  _16_bit_gateway u_16_bit_gateway_12 (.in_1(in_2), .in_2(in_1[4]), .out_3(n16_bit_gateway_12_out_3));
  _16_bit_shift_up u_16_bit_shift_up_24 (.in_1(n16_bit_gateway_12_out_3), .out_2(n16_bit_shift_up_24_out_2));
  _16_bit_shift_up u_16_bit_shift_up_25 (.in_1(n16_bit_gateway_13_out_3), .out_2(n16_bit_shift_up_25_out_2));
  _16_bit_shift_up u_16_bit_shift_up_26 (.in_1(n16_bit_shift_up_25_out_2), .out_2(n16_bit_shift_up_26_out_2));
  _16_bit_gateway u_16_bit_gateway_13 (.in_1(in_2), .in_2(in_1[3]), .out_3(n16_bit_gateway_13_out_3));
  _16_bit_shift_up u_16_bit_shift_up_27 (.in_1(n16_bit_gateway_14_out_3), .out_2(n16_bit_shift_up_27_out_2));
  _16_bit_shift_up u_16_bit_shift_up_28 (.in_1(n16_bit_shift_up_27_out_2), .out_2(n16_bit_shift_up_28_out_2));
  _16_bit_gateway u_16_bit_gateway_14 (.in_1(in_2), .in_2(in_1[2]), .out_3(n16_bit_gateway_14_out_3));
  _16_bit_gateway u_16_bit_gateway_15 (.in_1(in_2), .in_2(in_1[1]), .out_3(n16_bit_gateway_15_out_3));
  _16_bit_shift_up u_16_bit_shift_up_29 (.in_1(n16_bit_gateway_15_out_3), .out_2(n16_bit_shift_up_29_out_2));
  addition addition_1 (.in_1({16{1'b0}}), .in_2(n16_bit_gateway_16_out_3), .out_3(addition_1_out_3));
  _16_bit_gateway u_16_bit_gateway_16 (.in_1(in_2), .in_2(in_1[0]), .out_3(n16_bit_gateway_16_out_3));
  _16_bit_shift_up u_16_bit_shift_up_30 (.in_1(n16_bit_shift_up_31_out_2), .out_2(n16_bit_shift_up_30_out_2));
  _16_bit_shift_up u_16_bit_shift_up_31 (.in_1(n16_bit_shift_up_2_out_2), .out_2(n16_bit_shift_up_31_out_2));
  _16_bit_shift_up u_16_bit_shift_up_32 (.in_1(n16_bit_shift_up_30_out_2), .out_2(n16_bit_shift_up_32_out_2));
  _16_bit_shift_up u_16_bit_shift_up_33 (.in_1(n16_bit_shift_up_34_out_2), .out_2(n16_bit_shift_up_33_out_2));
  _16_bit_shift_up u_16_bit_shift_up_34 (.in_1(n16_bit_shift_up_3_out_2), .out_2(n16_bit_shift_up_34_out_2));
  _16_bit_shift_up u_16_bit_shift_up_35 (.in_1(n16_bit_shift_up_33_out_2), .out_2(n16_bit_shift_up_35_out_2));
  _16_bit_shift_up u_16_bit_shift_up_36 (.in_1(n16_bit_shift_up_38_out_2), .out_2(n16_bit_shift_up_36_out_2));
  _16_bit_shift_up u_16_bit_shift_up_37 (.in_1(n16_bit_shift_up_5_out_2), .out_2(n16_bit_shift_up_37_out_2));
  _16_bit_shift_up u_16_bit_shift_up_38 (.in_1(n16_bit_shift_up_37_out_2), .out_2(n16_bit_shift_up_38_out_2));
  _16_bit_shift_up u_16_bit_shift_up_39 (.in_1(n16_bit_shift_up_41_out_2), .out_2(n16_bit_shift_up_39_out_2));
  _16_bit_shift_up u_16_bit_shift_up_40 (.in_1(n16_bit_shift_up_39_out_2), .out_2(n16_bit_shift_up_40_out_2));
  _16_bit_shift_up u_16_bit_shift_up_41 (.in_1(n16_bit_shift_up_7_out_2), .out_2(n16_bit_shift_up_41_out_2));
  _16_bit_shift_up u_16_bit_shift_up_42 (.in_1(n16_bit_shift_up_44_out_2), .out_2(n16_bit_shift_up_42_out_2));
  _16_bit_shift_up u_16_bit_shift_up_43 (.in_1(n16_bit_shift_up_9_out_2), .out_2(n16_bit_shift_up_43_out_2));
  _16_bit_shift_up u_16_bit_shift_up_44 (.in_1(n16_bit_shift_up_43_out_2), .out_2(n16_bit_shift_up_44_out_2));
  _16_bit_shift_up u_16_bit_shift_up_45 (.in_1(n16_bit_shift_up_46_out_2), .out_2(n16_bit_shift_up_45_out_2));
  _16_bit_shift_up u_16_bit_shift_up_46 (.in_1(n16_bit_shift_up_47_out_2), .out_2(n16_bit_shift_up_46_out_2));
  _16_bit_shift_up u_16_bit_shift_up_47 (.in_1(n16_bit_shift_up_12_out_2), .out_2(n16_bit_shift_up_47_out_2));
  _16_bit_shift_up u_16_bit_shift_up_48 (.in_1(n16_bit_shift_up_49_out_2), .out_2(n16_bit_shift_up_48_out_2));
  _16_bit_shift_up u_16_bit_shift_up_49 (.in_1(n16_bit_shift_up_50_out_2), .out_2(n16_bit_shift_up_49_out_2));
  _16_bit_shift_up u_16_bit_shift_up_50 (.in_1(n16_bit_shift_up_13_out_2), .out_2(n16_bit_shift_up_50_out_2));
  _16_bit_shift_up u_16_bit_shift_up_51 (.in_1(n16_bit_shift_up_52_out_2), .out_2(n16_bit_shift_up_51_out_2));
  _16_bit_shift_up u_16_bit_shift_up_52 (.in_1(n16_bit_shift_up_16_out_2), .out_2(n16_bit_shift_up_52_out_2));
  _16_bit_shift_up u_16_bit_shift_up_53 (.in_1(n16_bit_shift_up_51_out_2), .out_2(n16_bit_shift_up_53_out_2));
  _16_bit_shift_up u_16_bit_shift_up_54 (.in_1(n16_bit_shift_up_56_out_2), .out_2(n16_bit_shift_up_54_out_2));
  _16_bit_shift_up u_16_bit_shift_up_55 (.in_1(n16_bit_shift_up_54_out_2), .out_2(n16_bit_shift_up_55_out_2));
  _16_bit_shift_up u_16_bit_shift_up_56 (.in_1(n16_bit_shift_up_17_out_2), .out_2(n16_bit_shift_up_56_out_2));
  _16_bit_shift_up u_16_bit_shift_up_57 (.in_1(n16_bit_shift_up_59_out_2), .out_2(n16_bit_shift_up_57_out_2));
  _16_bit_shift_up u_16_bit_shift_up_58 (.in_1(n16_bit_shift_up_57_out_2), .out_2(n16_bit_shift_up_58_out_2));
  _16_bit_shift_up u_16_bit_shift_up_59 (.in_1(n16_bit_shift_up_19_out_2), .out_2(n16_bit_shift_up_59_out_2));
  _16_bit_shift_up u_16_bit_shift_up_60 (.in_1(n16_bit_shift_up_22_out_2), .out_2(n16_bit_shift_up_60_out_2));
  _16_bit_shift_up u_16_bit_shift_up_61 (.in_1(n16_bit_shift_up_62_out_2), .out_2(n16_bit_shift_up_61_out_2));
  _16_bit_shift_up u_16_bit_shift_up_62 (.in_1(n16_bit_shift_up_60_out_2), .out_2(n16_bit_shift_up_62_out_2));
  _16_bit_shift_up u_16_bit_shift_up_63 (.in_1(n16_bit_shift_up_64_out_2), .out_2(n16_bit_shift_up_63_out_2));
  _16_bit_shift_up u_16_bit_shift_up_64 (.in_1(n16_bit_shift_up_23_out_2), .out_2(n16_bit_shift_up_64_out_2));
  addition addition_2 (.in_1(n16_bit_shift_up_65_out_2), .in_2(addition_3_out_3), .out_3(addition_2_out_3));
  _16_bit_shift_up u_16_bit_shift_up_65 (.in_1(n16_bit_shift_up_26_out_2), .out_2(n16_bit_shift_up_65_out_2));
  addition addition_3 (.in_1(n16_bit_shift_up_28_out_2), .in_2(addition_4_out_3), .out_3(addition_3_out_3));
  addition addition_4 (.in_1(n16_bit_shift_up_29_out_2), .in_2(addition_1_out_3), .out_3(addition_4_out_3));
  _16_bit_shift_up u_16_bit_shift_up_66 (.in_1(n16_bit_shift_up_67_out_2), .out_2(n16_bit_shift_up_66_out_2));
  _16_bit_shift_up u_16_bit_shift_up_67 (.in_1(n16_bit_shift_up_32_out_2), .out_2(n16_bit_shift_up_67_out_2));
  _16_bit_shift_up u_16_bit_shift_up_68 (.in_1(n16_bit_shift_up_35_out_2), .out_2(n16_bit_shift_up_68_out_2));
  _16_bit_shift_up u_16_bit_shift_up_69 (.in_1(n16_bit_shift_up_68_out_2), .out_2(n16_bit_shift_up_69_out_2));
  _16_bit_shift_up u_16_bit_shift_up_70 (.in_1(n16_bit_shift_up_71_out_2), .out_2(n16_bit_shift_up_70_out_2));
  _16_bit_shift_up u_16_bit_shift_up_71 (.in_1(n16_bit_shift_up_36_out_2), .out_2(n16_bit_shift_up_71_out_2));
  _16_bit_shift_up u_16_bit_shift_up_72 (.in_1(n16_bit_shift_up_40_out_2), .out_2(n16_bit_shift_up_72_out_2));
  _16_bit_shift_up u_16_bit_shift_up_73 (.in_1(n16_bit_shift_up_72_out_2), .out_2(n16_bit_shift_up_73_out_2));
  _16_bit_shift_up u_16_bit_shift_up_74 (.in_1(n16_bit_shift_up_75_out_2), .out_2(n16_bit_shift_up_74_out_2));
  _16_bit_shift_up u_16_bit_shift_up_75 (.in_1(n16_bit_shift_up_42_out_2), .out_2(n16_bit_shift_up_75_out_2));
  _16_bit_shift_up u_16_bit_shift_up_76 (.in_1(n16_bit_shift_up_77_out_2), .out_2(n16_bit_shift_up_76_out_2));
  _16_bit_shift_up u_16_bit_shift_up_77 (.in_1(n16_bit_shift_up_45_out_2), .out_2(n16_bit_shift_up_77_out_2));
  _16_bit_shift_up u_16_bit_shift_up_78 (.in_1(n16_bit_shift_up_48_out_2), .out_2(n16_bit_shift_up_78_out_2));
  _16_bit_shift_up u_16_bit_shift_up_79 (.in_1(n16_bit_shift_up_78_out_2), .out_2(n16_bit_shift_up_79_out_2));
  _16_bit_shift_up u_16_bit_shift_up_80 (.in_1(n16_bit_shift_up_81_out_2), .out_2(n16_bit_shift_up_80_out_2));
  _16_bit_shift_up u_16_bit_shift_up_81 (.in_1(n16_bit_shift_up_53_out_2), .out_2(n16_bit_shift_up_81_out_2));
  _16_bit_shift_up u_16_bit_shift_up_82 (.in_1(n16_bit_shift_up_83_out_2), .out_2(n16_bit_shift_up_82_out_2));
  _16_bit_shift_up u_16_bit_shift_up_83 (.in_1(n16_bit_shift_up_55_out_2), .out_2(n16_bit_shift_up_83_out_2));
  _16_bit_shift_up u_16_bit_shift_up_84 (.in_1(n16_bit_shift_up_58_out_2), .out_2(n16_bit_shift_up_84_out_2));
  addition addition_5 (.in_1(n16_bit_shift_up_61_out_2), .in_2(addition_6_out_3), .out_3(addition_5_out_3));
  addition addition_6 (.in_1(n16_bit_shift_up_63_out_2), .in_2(addition_2_out_3), .out_3(addition_6_out_3));
  _16_bit_shift_up u_16_bit_shift_up_85 (.in_1(n16_bit_shift_up_86_out_2), .out_2(n16_bit_shift_up_85_out_2));
  _16_bit_shift_up u_16_bit_shift_up_86 (.in_1(n16_bit_shift_up_87_out_2), .out_2(n16_bit_shift_up_86_out_2));
  _16_bit_shift_up u_16_bit_shift_up_87 (.in_1(n16_bit_shift_up_66_out_2), .out_2(n16_bit_shift_up_87_out_2));
  _16_bit_shift_up u_16_bit_shift_up_88 (.in_1(n16_bit_shift_up_69_out_2), .out_2(n16_bit_shift_up_88_out_2));
  _16_bit_shift_up u_16_bit_shift_up_89 (.in_1(n16_bit_shift_up_90_out_2), .out_2(n16_bit_shift_up_89_out_2));
  _16_bit_shift_up u_16_bit_shift_up_90 (.in_1(n16_bit_shift_up_88_out_2), .out_2(n16_bit_shift_up_90_out_2));
  _16_bit_shift_up u_16_bit_shift_up_91 (.in_1(n16_bit_shift_up_92_out_2), .out_2(n16_bit_shift_up_91_out_2));
  _16_bit_shift_up u_16_bit_shift_up_92 (.in_1(n16_bit_shift_up_70_out_2), .out_2(n16_bit_shift_up_92_out_2));
  _16_bit_shift_up u_16_bit_shift_up_93 (.in_1(n16_bit_shift_up_91_out_2), .out_2(n16_bit_shift_up_93_out_2));
  _16_bit_shift_up u_16_bit_shift_up_94 (.in_1(n16_bit_shift_up_96_out_2), .out_2(n16_bit_shift_up_94_out_2));
  _16_bit_shift_up u_16_bit_shift_up_95 (.in_1(n16_bit_shift_up_73_out_2), .out_2(n16_bit_shift_up_95_out_2));
  _16_bit_shift_up u_16_bit_shift_up_96 (.in_1(n16_bit_shift_up_95_out_2), .out_2(n16_bit_shift_up_96_out_2));
  _16_bit_shift_up u_16_bit_shift_up_97 (.in_1(n16_bit_shift_up_99_out_2), .out_2(n16_bit_shift_up_97_out_2));
  _16_bit_shift_up u_16_bit_shift_up_98 (.in_1(n16_bit_shift_up_97_out_2), .out_2(n16_bit_shift_up_98_out_2));
  _16_bit_shift_up u_16_bit_shift_up_99 (.in_1(n16_bit_shift_up_74_out_2), .out_2(n16_bit_shift_up_99_out_2));
  _16_bit_shift_up u_16_bit_shift_up_100 (.in_1(n16_bit_shift_up_102_out_2), .out_2(n16_bit_shift_up_100_out_2));
  _16_bit_shift_up u_16_bit_shift_up_101 (.in_1(n16_bit_shift_up_100_out_2), .out_2(n16_bit_shift_up_101_out_2));
  _16_bit_shift_up u_16_bit_shift_up_102 (.in_1(n16_bit_shift_up_76_out_2), .out_2(n16_bit_shift_up_102_out_2));
  _16_bit_shift_up u_16_bit_shift_up_103 (.in_1(n16_bit_shift_up_79_out_2), .out_2(n16_bit_shift_up_103_out_2));
  _16_bit_shift_up u_16_bit_shift_up_104 (.in_1(n16_bit_shift_up_103_out_2), .out_2(n16_bit_shift_up_104_out_2));
  _16_bit_shift_up u_16_bit_shift_up_105 (.in_1(n16_bit_shift_up_80_out_2), .out_2(n16_bit_shift_up_105_out_2));
  addition addition_7 (.in_1(n16_bit_shift_up_105_out_2), .in_2(addition_8_out_3), .out_3(addition_7_out_3));
  addition addition_8 (.in_1(n16_bit_shift_up_82_out_2), .in_2(addition_9_out_3), .out_3(addition_8_out_3));
  addition addition_9 (.in_1(n16_bit_shift_up_84_out_2), .in_2(addition_5_out_3), .out_3(addition_9_out_3));
  _16_bit_shift_up u_16_bit_shift_up_106 (.in_1(n16_bit_shift_up_85_out_2), .out_2(n16_bit_shift_up_106_out_2));
  _16_bit_shift_up u_16_bit_shift_up_107 (.in_1(n16_bit_shift_up_108_out_2), .out_2(n16_bit_shift_up_107_out_2));
  _16_bit_shift_up u_16_bit_shift_up_108 (.in_1(n16_bit_shift_up_106_out_2), .out_2(n16_bit_shift_up_108_out_2));
  _16_bit_shift_up u_16_bit_shift_up_109 (.in_1(n16_bit_shift_up_89_out_2), .out_2(n16_bit_shift_up_109_out_2));
  _16_bit_shift_up u_16_bit_shift_up_110 (.in_1(n16_bit_shift_up_109_out_2), .out_2(n16_bit_shift_up_110_out_2));
  _16_bit_shift_up u_16_bit_shift_up_111 (.in_1(n16_bit_shift_up_110_out_2), .out_2(n16_bit_shift_up_111_out_2));
  _16_bit_shift_up u_16_bit_shift_up_112 (.in_1(n16_bit_shift_up_114_out_2), .out_2(n16_bit_shift_up_112_out_2));
  _16_bit_shift_up u_16_bit_shift_up_113 (.in_1(n16_bit_shift_up_112_out_2), .out_2(n16_bit_shift_up_113_out_2));
  _16_bit_shift_up u_16_bit_shift_up_114 (.in_1(n16_bit_shift_up_93_out_2), .out_2(n16_bit_shift_up_114_out_2));
  _16_bit_shift_up u_16_bit_shift_up_115 (.in_1(n16_bit_shift_up_116_out_2), .out_2(n16_bit_shift_up_115_out_2));
  _16_bit_shift_up u_16_bit_shift_up_116 (.in_1(n16_bit_shift_up_94_out_2), .out_2(n16_bit_shift_up_116_out_2));
  _16_bit_shift_up u_16_bit_shift_up_117 (.in_1(n16_bit_shift_up_98_out_2), .out_2(n16_bit_shift_up_117_out_2));
  addition addition_10 (.in_1(n16_bit_shift_up_117_out_2), .in_2(addition_11_out_3), .out_3(addition_10_out_3));
  addition addition_11 (.in_1(n16_bit_shift_up_101_out_2), .in_2(addition_12_out_3), .out_3(addition_11_out_3));
  addition addition_12 (.in_1(n16_bit_shift_up_104_out_2), .in_2(addition_7_out_3), .out_3(addition_12_out_3));
  _16_bit_shift_up u_16_bit_shift_up_118 (.in_1(n16_bit_shift_up_119_out_2), .out_2(n16_bit_shift_up_118_out_2));
  _16_bit_shift_up u_16_bit_shift_up_119 (.in_1(n16_bit_shift_up_107_out_2), .out_2(n16_bit_shift_up_119_out_2));
  _16_bit_shift_up u_16_bit_shift_up_120 (.in_1(n16_bit_shift_up_111_out_2), .out_2(n16_bit_shift_up_120_out_2));
  addition addition_13 (.in_1(n16_bit_shift_up_113_out_2), .in_2(addition_14_out_3), .out_3(addition_13_out_3));
  addition addition_14 (.in_1(n16_bit_shift_up_115_out_2), .in_2(addition_10_out_3), .out_3(addition_14_out_3));
  addition addition_15 (.in_1(n16_bit_shift_up_118_out_2), .in_2(addition_16_out_3), .out_3(out_3));
  addition addition_16 (.in_1(n16_bit_shift_up_120_out_2), .in_2(addition_13_out_3), .out_3(addition_16_out_3));
endmodule

module _16_bit_shift_up (
  input  [15:0] in_1,
  output [15:0] out_2
);


  assign out_2 = {in_1[14:0], 1'b0};
endmodule

module binary_divide10 (
  input  [15:0] in_1,
  output [15:0] out_2,
  output [3:0] rem
);

  wire [31:0] n16_bit_to_32_bit_mult_1_out_3;

  _16_bit_to_32_bit_mult u_16_bit_to_32_bit_mult_1 (
    .in_1(in_1), .in_2(16'hccc),
    .out_3({n16_bit_to_32_bit_mult_1_out_3[31], out_2, rem, n16_bit_to_32_bit_mult_1_out_3[10:0]}));
endmodule

module _16_bit_to_32_bit_mult (
  input  [15:0] in_1,
  input  [15:0] in_2,
  output [31:0] out_3
);

  wire [15:0] multiplication_1_out_3, multiplication_2_out_3, multiplication_3_out_3, multiplication_4_out_3;
  wire [31:0] n32_bit_addition_1_out_3, n32_bit_addition_2_out_3;

  multiplication multiplication_1 (
    .in_1({{8{1'b0}}, in_1[7:0]}), .in_2({{8{1'b0}}, in_2[7:0]}), .out_3(multiplication_1_out_3));
  multiplication multiplication_2 (
    .in_1({{8{1'b0}}, in_1[15:8]}), .in_2({{8{1'b0}}, in_2[15:8]}), .out_3(multiplication_2_out_3));
  multiplication multiplication_3 (
    .in_1({{8{1'b0}}, in_2[7:0]}), .in_2({{8{1'b0}}, in_2[15:8]}), .out_3(multiplication_3_out_3));
  multiplication multiplication_4 (
    .in_1({{8{1'b0}}, in_1[15:8]}), .in_2({{8{1'b0}}, in_2[7:0]}), .out_3(multiplication_4_out_3));
  _32_bit_addition u_32_bit_addition_1 (
    .in_1({{16{1'b0}}, multiplication_1_out_3}), .in_2({multiplication_2_out_3, {16{1'b0}}}),
    .out_3(n32_bit_addition_1_out_3));
  _32_bit_addition u_32_bit_addition_2 (
    .in_1({{8{1'b0}}, multiplication_3_out_3, {8{1'b0}}}),
    .in_2({{8{1'b0}}, multiplication_4_out_3, {8{1'b0}}}), .out_3(n32_bit_addition_2_out_3));
  _32_bit_addition u_32_bit_addition_3 (
    .in_1(n32_bit_addition_1_out_3), .in_2(n32_bit_addition_2_out_3), .out_3(out_3));
endmodule

module _32_bit_addition (
  input  [31:0] in_1,
  input  [31:0] in_2,
  output [31:0] out_3
);

  wire n4_bit_sum_2_out_10, n4_bit_sum_3_out_10, n4_bit_sum_4_out_10, n4_bit_sum_5_out_10,
       n4_bit_sum_6_out_10, n4_bit_sum_7_out_10, n4_bit_sum_8_out_10;

  _4_bit_sum u_4_bit_sum_1 (
    .in_1(in_1[28]), .in_2(in_1[29]), .in_3(in_1[30]), .in_4(in_1[31]), .in_5(in_2[28]), .in_6(in_2[29]),
    .in_7(in_2[30]), .in_8(in_2[31]), .rin(n4_bit_sum_2_out_10), .out_11(out_3[28]), .out_12(out_3[29]),
    .out_13(out_3[30]), .out_14(out_3[31]));  // open: out_10
  _4_bit_sum u_4_bit_sum_2 (
    .in_1(in_1[24]), .in_2(in_1[25]), .in_3(in_1[26]), .in_4(in_1[27]), .in_5(in_2[24]), .in_6(in_2[25]),
    .in_7(in_2[26]), .in_8(in_2[27]), .out_10(n4_bit_sum_2_out_10), .rin(n4_bit_sum_3_out_10),
    .out_11(out_3[24]), .out_12(out_3[25]), .out_13(out_3[26]), .out_14(out_3[27]));
  _4_bit_sum u_4_bit_sum_3 (
    .in_1(in_1[20]), .in_2(in_1[21]), .in_3(in_1[22]), .in_4(in_1[23]), .in_5(in_2[20]), .in_6(in_2[21]),
    .in_7(in_2[22]), .in_8(in_2[23]), .out_10(n4_bit_sum_3_out_10), .rin(n4_bit_sum_4_out_10),
    .out_11(out_3[20]), .out_12(out_3[21]), .out_13(out_3[22]), .out_14(out_3[23]));
  _4_bit_sum u_4_bit_sum_4 (
    .in_1(in_1[16]), .in_2(in_1[17]), .in_3(in_1[18]), .in_4(in_1[19]), .in_5(in_2[16]), .in_6(in_2[17]),
    .in_7(in_2[18]), .in_8(in_2[19]), .out_10(n4_bit_sum_4_out_10), .rin(n4_bit_sum_5_out_10),
    .out_11(out_3[16]), .out_12(out_3[17]), .out_13(out_3[18]), .out_14(out_3[19]));
  _4_bit_sum u_4_bit_sum_5 (
    .in_1(in_1[12]), .in_2(in_1[13]), .in_3(in_1[14]), .in_4(in_1[15]), .in_5(in_2[12]), .in_6(in_2[13]),
    .in_7(in_2[14]), .in_8(in_2[15]), .out_10(n4_bit_sum_5_out_10), .rin(n4_bit_sum_6_out_10),
    .out_11(out_3[12]), .out_12(out_3[13]), .out_13(out_3[14]), .out_14(out_3[15]));
  _4_bit_sum u_4_bit_sum_6 (
    .in_1(in_1[8]), .in_2(in_1[9]), .in_3(in_1[10]), .in_4(in_1[11]), .in_5(in_2[8]), .in_6(in_2[9]),
    .in_7(in_2[10]), .in_8(in_2[11]), .out_10(n4_bit_sum_6_out_10), .rin(n4_bit_sum_7_out_10),
    .out_11(out_3[8]), .out_12(out_3[9]), .out_13(out_3[10]), .out_14(out_3[11]));
  _4_bit_sum u_4_bit_sum_7 (
    .in_1(in_1[4]), .in_2(in_1[5]), .in_3(in_1[6]), .in_4(in_1[7]), .in_5(in_2[4]), .in_6(in_2[5]),
    .in_7(in_2[6]), .in_8(in_2[7]), .out_10(n4_bit_sum_7_out_10), .rin(n4_bit_sum_8_out_10),
    .out_11(out_3[4]), .out_12(out_3[5]), .out_13(out_3[6]), .out_14(out_3[7]));
  _4_bit_sum u_4_bit_sum_8 (
    .in_1(in_1[0]), .in_2(in_1[1]), .in_3(in_1[2]), .in_4(in_1[3]), .in_5(in_2[0]), .in_6(in_2[1]),
    .in_7(in_2[2]), .in_8(in_2[3]), .out_10(n4_bit_sum_8_out_10), .rin(1'b0), .out_11(out_3[0]),
    .out_12(out_3[1]), .out_13(out_3[2]), .out_14(out_3[3]));
endmodule
